// Logisim project RV32I_SingleCycle.circ as structural Verilog: 12 circuits, main circuit RV32I_SingleCycle
module RV32I_SingleCycle (
  output halt,
  output [31:0] cycles,
  output [31:0] instret,
  output [31:0] pc,
  output [31:0] gpio
);

  wire Branch, branchunit_1_taken, BSel, CLK, f7b5, IO_kbdavail, IO_kbdre, IO_txwe, IsIO, Jal, Jalr, MemRead,
       MemWrite, PCEn, PCSel, RamWE, RegWrite;
  wire [1:0] ALUOp, ASel, Off, WBSel;
  wire [2:0] funct3, ImmSel;
  wire [3:0] ALUCtrl;
  wire [4:0] rd, rs1, rs2;
  wire [6:0] IO_kbddata, IO_txdata;
  wire [7:0] IO_gpioin;
  wire [11:0] WordAddr;
  wire [31:0] alu, imm, instr, IO_rdata, loaddata, memword, multiplexer_1_out, multiplexer_2_out,
       multiplexer_3_out, pc4, ramout, rs1d, rs2d, stnew, target, wbdata;

  Clock u_CLK (.out(CLK));
  Multiplexer #(.width(32), .select(1), .enable("false")) multiplexer_1 (
    .in0(pc4), .in1(target), .out(multiplexer_1_out), .sel(PCSel));
  Register #(.width(32)) u_PC (.D(multiplexer_1_out), .en(PCEn), .clk(CLK), .Q(pc), .clr(1'b0));
  not not_1 (PCEn, halt);
  Adder #(.width(32)) adder_1 (.a(pc), .b(32'h4), .out(pc4), .cin(1'b0));  // open: cout
  ROM #(.addrWidth(10), .dataWidth(32)) IMEM (.addr(pc[11:2]), .data(instr));
  PerfCounters perfcounters_1 (.CLK(CLK), .Run(PCEn), .Retire(1'b1), .cycles(cycles), .instret(instret));
  Control control_1 (
    .Instr(instr), .rd(rd), .rs1(rs1), .rs2(rs2), .funct3(funct3), .f7b5(f7b5), .RegWrite(RegWrite),
    .ASel(ASel), .BSel(BSel), .ALUOp(ALUOp), .ImmSel(ImmSel), .MemRead(MemRead), .MemWrite(MemWrite),
    .WBSel(WBSel), .Branch(Branch), .Jal(Jal), .Jalr(Jalr), .Halt(halt));  // open: UseRs1, UseRs2
  // Probe on instr
  RegisterFile registerfile_1 (
    .RA1(rs1), .RA2(rs2), .WA(rd), .WD(wbdata), .WE(RegWrite), .CLK(CLK), .RD1(rs1d), .RD2(rs2d));
  ImmGen immgen_1 (.Instr(instr), .ImmSel(ImmSel), .Imm(imm));
  ALUControl alucontrol_1 (.ALUOp(ALUOp), .funct3(funct3), .f7b5(f7b5), .ALUCtrl(ALUCtrl));
  Multiplexer #(.width(32), .select(2), .enable("false")) multiplexer_2 (
    .in0(rs1d), .in1(pc), .in2({32{1'b0}}), .in3({32{1'b0}}), .out(multiplexer_2_out), .sel(ASel));
  Multiplexer #(.width(32), .select(1), .enable("false")) multiplexer_3 (
    .in0(rs2d), .in1(imm), .out(multiplexer_3_out), .sel(BSel));
  ALU alu_1 (.A(multiplexer_2_out), .B(multiplexer_3_out), .Y(alu), .ALUCtrl(ALUCtrl));
  BranchUnit branchunit_1 (.A(rs1d), .B(rs2d), .funct3(funct3), .Branch(Branch), .Taken(branchunit_1_taken));
  // Probe on alu
  or or_1 (PCSel, Jal, Jalr, branchunit_1_taken);
  assign target = alu & 32'hfffffffe;  // AND_Gate and_1, 32 bits wide
  AddrDecode addrdecode_1 (
    .Addr(alu), .MemWrite(MemWrite), .WordAddr(WordAddr), .Off(Off), .RamWE(RamWE), .IsIO(IsIO));  // open: IoWE
  StoreUnit storeunit_1 (.Old(memword), .WData(rs2d), .Off(Off), .funct3(funct3), .New(stnew));
  IOController iocontroller_1 (
    .Addr(alu), .WData(stnew), .MemWrite(MemWrite), .MemRead(MemRead), .IsIO(IsIO), .CLK(CLK),
    .KbdData(IO_kbddata), .KbdAvail(IO_kbdavail), .GpioIn(IO_gpioin), .IoRData(IO_rdata), .TxWE(IO_txwe),
    .TxData(IO_txdata), .KbdRE(IO_kbdre), .GpioOut(gpio));
  DipSwitch #(.number(8)) dipswitch_1 (
    .sw1(IO_gpioin[7]), .sw2(IO_gpioin[6]), .sw3(IO_gpioin[5]), .sw4(IO_gpioin[4]), .sw5(IO_gpioin[3]),
    .sw6(IO_gpioin[2]), .sw7(IO_gpioin[1]), .sw8(IO_gpioin[0]));
  RAM #(.addrWidth(12), .dataWidth(32), .asyncread("true"), .databus("bibus")) DMEM (
    .addr(WordAddr), .we(RamWE), .oe(1'b1), .clk(CLK), .din(stnew), .dout(ramout));
  Multiplexer #(.width(32), .select(1), .enable("false")) multiplexer_4 (
    .in0(ramout), .in1(IO_rdata), .out(memword), .sel(IsIO));
  TTY #(.rows(8), .cols(32)) tty_1 (.data(IO_txdata), .clk(CLK), .we(IO_txwe), .clr(1'b0));
  Keyboard #(.buflen(32)) keyboard_1 (.clk(CLK), .re(IO_kbdre), .clr(1'b0), .avail(IO_kbdavail), .data(IO_kbddata));
  LoadUnit loadunit_1 (.Word(memword), .Off(Off), .funct3(funct3), .Data(loaddata));
  Multiplexer #(.width(32), .select(2), .enable("false")) multiplexer_5 (
    .in0(alu), .in1(loaddata), .in2(pc4), .in3({32{1'b0}}), .out(wbdata), .sel(WBSel));
  // Probe on wbdata
  Hex_Digit_Display #(.decimalPoint("false")) hex_digit_display_1 (.value(gpio[15:12]));
  Hex_Digit_Display #(.decimalPoint("false")) hex_digit_display_2 (.value(gpio[11:8]));
  Hex_Digit_Display #(.decimalPoint("false")) hex_digit_display_3 (.value(gpio[7:4]));
  // LedBar #(.matrixcols(8), .inputtype("row")) ledbar_1: pin names not known; wires that end beside it: gpio[23:16]
  Hex_Digit_Display #(.decimalPoint("false")) hex_digit_display_4 (.value(gpio[3:0]));

  // Other names for the same wires on the sheet: IO_gpio[31:0] = gpio; IO_hex3[3:0] = gpio[3:0];
  //   IO_hex2[3:0] = gpio[7:4]; IO_hex1[3:0] = gpio[11:8]; IO_hex0[3:0] = gpio[15:12]; IO_led[7:0] = gpio[23:16]

  // Notes on the sheet:
  //   RV32I SINGLE-CYCLE CPU  (moi lenh chay xong trong 1 chu ky clock)
  //   Chay: Simulate > Ticks Enabled (Ctrl+K) hoac nhan Ctrl+T de tung nua chu ky.  Reset: Ctrl+R
  //   Nap chuong trinh: chuot phai ROM "IMEM" > Load Image... chon file *.text.hex (tools/rvasm.py)
  //   CPU dung khi gap EBREAK/ECALL (halt = 1).  I/O: 0xF0000000 UART TX (TTY), 0xF0000004 RX (Keyboard), 0xF0000010 GPIO_OUT, 0xF0000014 GPIO_IN
  //   next PC
  //   FETCH
  //   PCEn = !Halt (dung PC khi gap EBREAK)
  //   PC + 4
  //   PC[11:2]
  //   (word index)
  //   contents of IMEM (hex, n*v repeats v):
  //   4137 ff010113 437 40413 293 100313 c00393 542023 628e33 30293 e0313 440413 fff38393 fe0394e3 437
  //   40413 513 c00393 42e83 1d50533 440413 fff38393 fe0398e3 f00004b7 48493 4800f13 1e48023 6500f13
  //   1e48023 6c00f13 1e48023 6c00f13 1e48023 6f00f13 1e48023 2000f13 1e48023 5200f13 1e48023 4900f13
  //   1e48023 5300f13 1e48023 4300f13 1e48023 2d00f13 1e48023 5600f13 1e48023 2100f13 1e48023 a00f13
  //   1e48023 a4a823 ff00f13 1e48923 100073
  //   DECODE / REGISTER READ
  //   ASel: 0 rs1, 1 PC, 2 zero
  //   BSel: 0 rs2, 1 imm
  //   EXECUTE
  //   PCSel = Taken | Jal | Jalr
  //   target = ALU & ~1 (branch/JAL: PC+imm, JALR: rs1+imm)
  //   MEMORY
  //   GPIO_IN: 8 DIP switch (0xF0000014), trai = bit 7
  //   IsIO ? I/O : RAM
  //   UART TX: TTY  (0xF0000000)
  //   UART RX: Keyboard (0xF0000004)
  //   STATUS 0xF0000008. Click vao Keyboard roi go phim
  //   WRITE BACK
  //   WBSel: 0 ALU, 1 Mem, 2 PC+4
  //   GPIO_OUT (0xF0000010): [15:0] hex, [23:16] LED
endmodule

module Control (
  input  [31:0] Instr,
  output [4:0] rd,
  output [4:0] rs1,
  output [4:0] rs2,
  output [2:0] funct3,
  output f7b5,
  output RegWrite,
  output [1:0] ASel,
  output BSel,
  output [1:0] ALUOp,
  output [2:0] ImmSel,
  output MemRead,
  output MemWrite,
  output [1:0] WBSel,
  output Branch,
  output Jal,
  output Jalr,
  output Halt,
  output UseRs1,
  output UseRs2
);

  wire decoder_1_out5, decoder_1_out12, valid;

  and and_1 (valid, Instr[0], Instr[1]);
  Decoder #(.select(5), .enable("true")) decoder_1 (
    .out0(MemRead), .out4(ALUOp[0]), .out5(decoder_1_out5), .out8(MemWrite), .out12(decoder_1_out12),
    .out13(ASel[1]), .out24(Branch), .out25(Jalr), .out27(ImmSel[2]), .out28(Halt), .sel(Instr[6:2]),
    .en(valid));  // open: out1, out2, out3, out6, out7, out9, out10, out11, out14, out15, out16, out17, out18, out19, out20, out21, out22, out23, out26, out29, out30, out31
  or or_1 (RegWrite, decoder_1_out12, ALUOp[0], MemRead, ImmSel[2], Jalr, ASel[1], decoder_1_out5);
  or or_2 (ASel[0], Branch, ImmSel[2], decoder_1_out5);
  or or_3 (BSel, ALUOp[0], MemRead, MemWrite, Branch, ImmSel[2], Jalr, ASel[1], decoder_1_out5);
  or or_4 (ALUOp[1], decoder_1_out12, ALUOp[0]);
  or or_5 (ImmSel[0], MemWrite, ASel[1], decoder_1_out5);
  or or_6 (ImmSel[1], Branch, ASel[1], decoder_1_out5);
  or or_7 (WBSel[1], ImmSel[2], Jalr);
  or or_8 (UseRs1, decoder_1_out12, ALUOp[0], MemRead, MemWrite, Branch, Jalr);
  or or_9 (UseRs2, decoder_1_out12, MemWrite, Branch);

  assign f7b5 = Instr[30];
  assign funct3 = Instr[14:12];
  assign Jal = ImmSel[2];
  assign rd = Instr[11:7];
  assign rs1 = Instr[19:15];
  assign rs2 = Instr[24:20];
  assign WBSel[0] = MemRead;

  // Other names for the same wires on the sheet: q0 = Instr[0]; q1 = Instr[1]; opc[4:0] = Instr[6:2];
  //   WBSel0 = MemRead

  // Notes on the sheet:
  //   Control Unit (Main Decoder) - ve theo kieu PLA:
  //   1) Decoder 5->32 bien opcode[6:2] thanh 1 duong "one-hot" cho moi nhom lenh (chi bat khi opcode[1:0]=11)
  //   2) Moi tin hieu dieu khien = OR cua cac nhom lenh can no (cot doc = nhom lenh, cham tron = co noi)
  //   Lenh = 0x00000000 (bubble) -> opcode[1:0]=00 -> decoder tat -> moi tin hieu = 0 = NOP
  //   tach truong lenh
  //   valid = opcode[1:0]==11
  //   opcode[6:2]
  //   JAL
  //   SYSTEM
  //   BRANCH
  //   JALR
  //   OP
  //   LUI
  //   AUIPC
  //   STORE
  //   LOAD
  //   OPIMM
  //   Bang chan ly (1 = bat):
  //   nhom     opcode  RegW ASel BSel ALUOp ImmSel MemR MemW WBSel
  //   OP       0110011  1    00   0    10    -      0    0    00
  //   OP-IMM   0010011  1    00   1    11    I      0    0    00
  //   LOAD     0000011  1    00   1    00    I      1    0    01
  //   STORE    0100011  0    00   1    00    S      0    1    --
  //   BRANCH   1100011  0    01   1    00    B      0    0    --
  //   JAL      1101111  1    01   1    00    J      0    0    10
  //   JALR     1100111  1    00   1    00    I      0    0    10
  //   LUI      0110111  1    10   1    00    U      0    0    00
  //   AUIPC    0010111  1    01   1    00    U      0    0    00
  //   SYSTEM   1110011  0  (Halt = 1: ECALL/EBREAK dung CPU)
  //   ASel: 0=rs1 1=PC 2=0   WBSel: 0=ALU 1=Mem 2=PC+4
  //   ImmSel: 0=I 1=S 2=B 3=U 4=J
endmodule

module RegisterFile (
  input  [4:0] RA1,
  input  [4:0] RA2,
  input  [4:0] WA,
  input  [31:0] WD,
  input  WE,
  input  CLK,
  output [31:0] RD1,
  output [31:0] RD2
);

  wire we1, we2, we3, we4, we5, we6, we7, we8, we9, we10, we11, we12, we13, we14, we15, we16, we17, we18,
       we19, we20, we21, we22, we23, we24, we25, we26, we27, we28, we29, we30, we31;
  wire [31:0] x1, x2, x3, x4, x5, x6, x7, x8, x9, x10, x11, x12, x13, x14, x15, x16, x17, x18, x19, x20, x21,
       x22, x23, x24, x25, x26, x27, x28, x29, x30, x31;

  Decoder #(.select(5), .enable("true")) decoder_1 (
    .out1(we1), .out2(we2), .out3(we3), .out4(we4), .out5(we5), .out6(we6), .out7(we7), .out8(we8),
    .out9(we9), .out10(we10), .out11(we11), .out12(we12), .out13(we13), .out14(we14), .out15(we15),
    .out16(we16), .out17(we17), .out18(we18), .out19(we19), .out20(we20), .out21(we21), .out22(we22),
    .out23(we23), .out24(we24), .out25(we25), .out26(we26), .out27(we27), .out28(we28), .out29(we29),
    .out30(we30), .out31(we31), .sel(WA), .en(WE));  // open: out0
  Register #(.width(32)) x1_ra (.D(WD), .en(we1), .clk(CLK), .Q(x1), .clr(1'b0));
  Register #(.width(32)) x2_sp (.D(WD), .en(we2), .clk(CLK), .Q(x2), .clr(1'b0));
  Register #(.width(32)) x3_gp (.D(WD), .en(we3), .clk(CLK), .Q(x3), .clr(1'b0));
  Register #(.width(32)) x4_tp (.D(WD), .en(we4), .clk(CLK), .Q(x4), .clr(1'b0));
  Register #(.width(32)) x5_t0 (.D(WD), .en(we5), .clk(CLK), .Q(x5), .clr(1'b0));
  Register #(.width(32)) x6_t1 (.D(WD), .en(we6), .clk(CLK), .Q(x6), .clr(1'b0));
  Register #(.width(32)) x7_t2 (.D(WD), .en(we7), .clk(CLK), .Q(x7), .clr(1'b0));
  Register #(.width(32)) x8_s0 (.D(WD), .en(we8), .clk(CLK), .Q(x8), .clr(1'b0));
  Register #(.width(32)) x9_s1 (.D(WD), .en(we9), .clk(CLK), .Q(x9), .clr(1'b0));
  Register #(.width(32)) x10_a0 (.D(WD), .en(we10), .clk(CLK), .Q(x10), .clr(1'b0));
  Register #(.width(32)) x11_a1 (.D(WD), .en(we11), .clk(CLK), .Q(x11), .clr(1'b0));
  Register #(.width(32)) x12_a2 (.D(WD), .en(we12), .clk(CLK), .Q(x12), .clr(1'b0));
  Register #(.width(32)) x13_a3 (.D(WD), .en(we13), .clk(CLK), .Q(x13), .clr(1'b0));
  Register #(.width(32)) x14_a4 (.D(WD), .en(we14), .clk(CLK), .Q(x14), .clr(1'b0));
  Register #(.width(32)) x15_a5 (.D(WD), .en(we15), .clk(CLK), .Q(x15), .clr(1'b0));
  Register #(.width(32)) x16_a6 (.D(WD), .en(we16), .clk(CLK), .Q(x16), .clr(1'b0));
  Register #(.width(32)) x17_a7 (.D(WD), .en(we17), .clk(CLK), .Q(x17), .clr(1'b0));
  Register #(.width(32)) x18_s2 (.D(WD), .en(we18), .clk(CLK), .Q(x18), .clr(1'b0));
  Register #(.width(32)) x19_s3 (.D(WD), .en(we19), .clk(CLK), .Q(x19), .clr(1'b0));
  Register #(.width(32)) x20_s4 (.D(WD), .en(we20), .clk(CLK), .Q(x20), .clr(1'b0));
  Register #(.width(32)) x21_s5 (.D(WD), .en(we21), .clk(CLK), .Q(x21), .clr(1'b0));
  Register #(.width(32)) x22_s6 (.D(WD), .en(we22), .clk(CLK), .Q(x22), .clr(1'b0));
  Register #(.width(32)) x23_s7 (.D(WD), .en(we23), .clk(CLK), .Q(x23), .clr(1'b0));
  Register #(.width(32)) x24_s8 (.D(WD), .en(we24), .clk(CLK), .Q(x24), .clr(1'b0));
  Register #(.width(32)) x25_s9 (.D(WD), .en(we25), .clk(CLK), .Q(x25), .clr(1'b0));
  Register #(.width(32)) x26_s10 (.D(WD), .en(we26), .clk(CLK), .Q(x26), .clr(1'b0));
  Register #(.width(32)) x27_s11 (.D(WD), .en(we27), .clk(CLK), .Q(x27), .clr(1'b0));
  Register #(.width(32)) x28_t3 (.D(WD), .en(we28), .clk(CLK), .Q(x28), .clr(1'b0));
  Register #(.width(32)) x29_t4 (.D(WD), .en(we29), .clk(CLK), .Q(x29), .clr(1'b0));
  Register #(.width(32)) x30_t5 (.D(WD), .en(we30), .clk(CLK), .Q(x30), .clr(1'b0));
  Register #(.width(32)) x31_t6 (.D(WD), .en(we31), .clk(CLK), .Q(x31), .clr(1'b0));
  Multiplexer #(.width(32), .select(5), .enable("false")) multiplexer_1 (
    .in0({32{1'b0}}), .in1(x1), .in2(x2), .in3(x3), .in4(x4), .in5(x5), .in6(x6), .in7(x7), .in8(x8),
    .in9(x9), .in10(x10), .in11(x11), .in12(x12), .in13(x13), .in14(x14), .in15(x15), .in16(x16), .in17(x17),
    .in18(x18), .in19(x19), .in20(x20), .in21(x21), .in22(x22), .in23(x23), .in24(x24), .in25(x25),
    .in26(x26), .in27(x27), .in28(x28), .in29(x29), .in30(x30), .in31(x31), .out(RD1), .sel(RA1));
  Multiplexer #(.width(32), .select(5), .enable("false")) multiplexer_2 (
    .in0({32{1'b0}}), .in1(x1), .in2(x2), .in3(x3), .in4(x4), .in5(x5), .in6(x6), .in7(x7), .in8(x8),
    .in9(x9), .in10(x10), .in11(x11), .in12(x12), .in13(x13), .in14(x14), .in15(x15), .in16(x16), .in17(x17),
    .in18(x18), .in19(x19), .in20(x20), .in21(x21), .in22(x22), .in23(x23), .in24(x24), .in25(x25),
    .in26(x26), .in27(x27), .in28(x28), .in29(x29), .in30(x30), .in31(x31), .out(RD2), .sel(RA2));

  // Notes on the sheet:
  //   Register File 32 x 32-bit: 2 cong doc (to hop, khong can clock) + 1 cong ghi (canh len CLK)
  //   Ghi: Decoder 5->32 bien WA thanh one-hot, AND voi WE -> chi 1 thanh ghi duoc bat Enable
  //   Doc: 2 MUX 32->1 chon theo RA1/RA2.  x0 khong phai thanh ghi: dau vao 0 cua MUX noi hang so 0
  //   write decoder
  //   x0 (zero)
  //   khong luu tru:
  //   doc luon = 0
  //   read port 1
  //   read port 2
endmodule

module ImmGen (
  input  [31:0] Instr,
  input  [2:0] ImmSel,
  output [31:0] Imm
);

  wire [31:0] bit_extender_1_out, bit_extender_2_out, bit_extender_3_out, bit_extender_4_out;

  assign bit_extender_1_out = {{20{Instr[31]}}, Instr[31:20]};  // Bit_Extender bit_extender_1
  assign bit_extender_2_out = {{20{Instr[31]}}, {Instr[31:25], Instr[11:7]}};  // Bit_Extender bit_extender_2
  assign bit_extender_3_out = {{19{Instr[31]}}, {Instr[31], Instr[7], Instr[30:25], Instr[11:8], 1'b0}};  // Bit_Extender bit_extender_3
  assign bit_extender_4_out = {{11{Instr[31]}}, {Instr[31], Instr[19:12], Instr[20], Instr[30:21], 1'b0}};  // Bit_Extender bit_extender_4
  Multiplexer #(.width(32), .select(3), .enable("false")) multiplexer_1 (
    .in0(bit_extender_1_out), .in1(bit_extender_2_out), .in2(bit_extender_3_out),
    .in3({Instr[31:12], {12{1'b0}}}), .in4(bit_extender_4_out), .in5({32{1'b0}}), .in6({32{1'b0}}),
    .in7({32{1'b0}}), .out(Imm), .sel(ImmSel));

  // Other names for the same wires on the sheet: i11_8[3:0] = Instr[11:8]; i7 = Instr[7]; i24_21[3:0] = Instr[24:21];
  //   i30_25[5:0] = Instr[30:25]; i20 = Instr[20]; i14_12[2:0] = Instr[14:12]; i19_15[4:0] = Instr[19:15];
  //   i31 = Instr[31]

  // Notes on the sheet:
  //   Immediate Generator: ghep cac manh bit cua lenh thanh hang so 32-bit (sign-extend)
  //   RISC-V co tinh "xao tron" bit cua B/J-type de bit dau (inst[31]) luon la bit dau cua imm
  //   va cac manh bit nam o cung vi tri giua cac dang lenh -> phan cung chi can noi day + MUX.
  //   ImmSel: 0=I  1=S  2=B  3=U  4=J
  //   inst[7]
  //   inst[11:8]
  //   inst[14:12]
  //   inst[19:15]
  //   inst[20]
  //   inst[24:21]
  //   inst[30:25]
  //   inst[31]
  //   I-type  imm[11:0]
  //   S-type  imm[11:0]
  //   B-type  imm[12:0]
  //   U-type  imm[31:0]
  //   J-type  imm[20:0]
  //   ImmSel: 0=I 1=S 2=B 3=U 4=J
endmodule

module ALUControl (
  input  [1:0] ALUOp,
  input  [2:0] funct3,
  input  f7b5,
  output [3:0] ALUCtrl
);

  wire comparator_1_eq, or_1_out;

  Multiplexer #(.width(3), .select(1), .enable("false")) multiplexer_1 (
    .in0(3'b000), .in1(funct3), .out(ALUCtrl[2:0]), .sel(ALUOp[1]));
  Comparator #(.width(3), .mode("unsigned")) comparator_1 (
    .a(funct3), .b(3'b101), .eq(comparator_1_eq));  // open: gt, lt
  or or_1 (or_1_out, ~ALUOp[0], comparator_1_eq);  // OR_Gate
  and and_1 (ALUCtrl[3], ALUOp[1], f7b5, or_1_out);

  // Other names for the same wires on the sheet: op[2:0] = ALUCtrl[2:0]; alt = ALUCtrl[3]

  // Notes on the sheet:
  //   ALU Control: (ALUOp, funct3, bit30) -> ALUCtrl[3:0] = {alt, op}
  //   ALUOp 00: ADD (load/store/branch/jump/lui/auipc)   10: R-type   11: I-type
  //   R-type: alt = bit30 (SUB/SRA).  I-type: alt = bit30 CHI KHI funct3=101 (SRAI);
  //   voi ADDI bit30 la mot phan cua immediate nen phai bo qua (khong co SUBI).
  //   op = ALUOp[1] ? funct3 : 000
  //   funct3 == 101 ?
endmodule

module ALU (
  input  [31:0] A,
  input  [31:0] B,
  input  [3:0] ALUCtrl,
  output [31:0] Y
);

  wire comparator_1_lt, comparator_2_lt;
  wire [31:0] adder_1_out, and_1_out, bit_extender_1_out, bit_extender_2_out, multiplexer_1_out,
       multiplexer_2_out, or_1_out, shifter_1_out, shifter_2_out, shifter_3_out, subtractor_1_out, xor_1_out;

  Adder #(.width(32)) adder_1 (.a(A), .b(B), .out(adder_1_out), .cin(1'b0));  // open: cout
  Subtractor #(.width(32)) subtractor_1 (.a(A), .b(B), .out(subtractor_1_out), .bin(1'b0));  // open: bout
  Comparator #(.width(32), .mode("twosComplement")) comparator_1 (.a(A), .b(B), .lt(comparator_1_lt));  // open: gt, eq
  assign bit_extender_1_out = {{31{1'b0}}, comparator_1_lt};  // Bit_Extender bit_extender_1
  Comparator #(.width(32), .mode("unsigned")) comparator_2 (.a(A), .b(B), .lt(comparator_2_lt));  // open: gt, eq
  assign bit_extender_2_out = {{31{1'b0}}, comparator_2_lt};  // Bit_Extender bit_extender_2
  assign xor_1_out = A ^ B;  // XOR_Gate xor_1, 32 bits wide
  assign or_1_out = A | B;  // OR_Gate or_1, 32 bits wide
  assign and_1_out = A & B;  // AND_Gate and_1, 32 bits wide
  Shifter #(.width(32), .shift("ll")) shifter_1 (.in(A), .\dist (B[4:0]), .out(shifter_1_out));
  Shifter #(.width(32), .shift("lr")) shifter_2 (.in(A), .\dist (B[4:0]), .out(shifter_2_out));
  Shifter #(.width(32), .shift("ar")) shifter_3 (.in(A), .\dist (B[4:0]), .out(shifter_3_out));
  Multiplexer #(.width(32), .select(1), .enable("false")) multiplexer_1 (
    .in0(adder_1_out), .in1(subtractor_1_out), .out(multiplexer_1_out), .sel(ALUCtrl[3]));
  Multiplexer #(.width(32), .select(1), .enable("false")) multiplexer_2 (
    .in0(shifter_2_out), .in1(shifter_3_out), .out(multiplexer_2_out), .sel(ALUCtrl[3]));
  Multiplexer #(.width(32), .select(3), .enable("false")) multiplexer_3 (
    .in0(multiplexer_1_out), .in1(shifter_1_out), .in2(bit_extender_1_out), .in3(bit_extender_2_out),
    .in4(xor_1_out), .in5(multiplexer_2_out), .in6(or_1_out), .in7(and_1_out), .out(Y), .sel(ALUCtrl[2:0]));

  // Other names for the same wires on the sheet: op[2:0] = ALUCtrl[2:0]; alt = ALUCtrl[3]; shamt[4:0] = B[4:0]

  // Notes on the sheet:
  //   ALU 32-bit  (Arithmetic Logic Unit)
  //   ALUCtrl = {bit30, funct3}: ma hoa trung voi funct3 cua RISC-V -> ALUControl gan nhu chi la "noi day"
  //   tach ALUCtrl
  //   shamt = B[4:0]
  //   ADD
  //   SUB
  //   SLT
  //   SLTU
  //   XOR
  //   OR
  //   AND
  //   SLL
  //   SRL
  //   SRA
  //   alt=0: ADD  alt=1: SUB
  //   alt=0: SRL  alt=1: SRA
  //   op=0 ADD/SUB
  //   op=1 SLL
  //   op=2 SLT
  //   op=3 SLTU
  //   op=4 XOR
  //   op=5 SRL/SRA
  //   op=6 OR
  //   op=7 AND
endmodule

module BranchUnit (
  input  [31:0] A,
  input  [31:0] B,
  input  [2:0] funct3,
  input  Branch,
  output Taken
);

  wire comparator_1_eq, comparator_2_lt, ltu, multiplexer_1_out, xor_1_out;

  Comparator #(.width(32), .mode("unsigned")) comparator_1 (.a(A), .b(B), .eq(comparator_1_eq), .lt(ltu));  // open: gt
  Comparator #(.width(32), .mode("twosComplement")) comparator_2 (.a(A), .b(B), .lt(comparator_2_lt));  // open: gt, eq
  Multiplexer #(.width(1), .select(2), .enable("false")) multiplexer_1 (
    .in0(comparator_1_eq), .in1(1'b0), .in2(comparator_2_lt), .in3(ltu), .out(multiplexer_1_out),
    .sel(funct3[2:1]));
  xor xor_1 (xor_1_out, multiplexer_1_out, funct3[0]);
  and and_1 (Taken, xor_1_out, Branch);

  // Other names for the same wires on the sheet: inv = funct3[0]; kind[1:0] = funct3[2:1]

  // Notes on the sheet:
  //   Branch Unit: quyet dinh re nhanh (BEQ BNE BLT BGE BLTU BGEU)
  //   funct3[2:1] chon phep so sanh: 00 = (A==B), 10 = A<B co dau, 11 = A<B khong dau
  //   funct3[0] = 1 dao nguoc ket qua: BNE = !BEQ, BGE = !BLT, BGEU = !BLTU
  //   Taken = Branch AND cond
  //   unsigned
  //   signed (bu 2)
endmodule

module AddrDecode (
  input  [31:0] Addr,
  input  MemWrite,
  output [11:0] WordAddr,
  output [1:0] Off,
  output RamWE,
  output IoWE,
  output IsIO
);

  Comparator #(.width(4), .mode("unsigned")) comparator_1 (.a(Addr[31:28]), .b(4'b1111), .eq(IsIO));  // open: gt, lt
  and and_1 (RamWE, MemWrite, ~IsIO);  // AND_Gate
  and and_2 (IoWE, MemWrite, IsIO);

  assign Off = Addr[1:0];
  assign WordAddr = Addr[13:2];

  // Other names for the same wires on the sheet: top[3:0] = Addr[31:28]

  // Notes on the sheet:
  //   Address Decoder (memory map):
  //   0x0000_0000-0x0000_3FFF : RAM 16 KiB  -> word address = Addr[13:2] (4096 tu 32-bit)
  //   0xF000_0000-0xFFFF_FFFF : I/O (TTY)   -> ghi 1 byte ra man hinh TTY
  //   Addr[1:0] = byte offset trong 1 word (dung cho LB/LH/SB/SH)
  //   Addr[31:28] == 0xF ?
endmodule

module StoreUnit (
  input  [31:0] Old,
  input  [31:0] WData,
  input  [1:0] Off,
  input  [2:0] funct3,
  output [31:0] New
);

  wire [31:0] and_1_out, and_2_out, D, M, multiplexer_1_out;

  Multiplexer #(.width(32), .select(2), .enable("false")) multiplexer_1 (
    .in0(32'hff), .in1(32'hffff), .in2({32{1'b1}}), .in3({32{1'b1}}), .out(multiplexer_1_out),
    .sel(funct3[1:0]));
  Shifter #(.width(32), .shift("ll")) shifter_1 (.in(multiplexer_1_out), .\dist ({Off, 3'b000}), .out(M));
  Shifter #(.width(32), .shift("ll")) shifter_2 (.in(WData), .\dist ({Off, 3'b000}), .out(D));
  assign and_1_out = Old & ~M;  // AND_Gate and_1, 32 bits wide
  assign and_2_out = D & M;  // AND_Gate and_2, 32 bits wide
  assign New = and_1_out | and_2_out;  // OR_Gate or_1, 32 bits wide

  // Other names for the same wires on the sheet: size[1:0] = funct3[1:0]; sh[4:3] = Off

  // Notes on the sheet:
  //   Store Unit (read-modify-write): RAM chi ghi duoc ca word 32-bit,
  //   nen voi SB/SH ta doc word cu (Old), thay dung byte/halfword roi ghi lai ca word.
  //   M = mask (0xFF / 0xFFFF / 0xFFFFFFFF) << sh ;  New = (Old AND ~M) OR ((WData << sh) AND M)
  //   sh = Off * 8 = {Off,000}
  //   size: 00=SB 01=SH 10=SW
  //   Old AND ~M (giu byte khac)
  //   D AND M (byte moi)
endmodule

module LoadUnit (
  input  [31:0] Word,
  input  [1:0] Off,
  input  [2:0] funct3,
  output [31:0] Data
);

  wire [31:0] bit_extender_1_out, bit_extender_2_out, bit_extender_3_out, bit_extender_4_out, S;

  Shifter #(.width(32), .shift("lr")) shifter_1 (.in(Word), .\dist ({Off, 3'b000}), .out(S));
  assign bit_extender_1_out = {{24{S[7]}}, S[7:0]};  // Bit_Extender bit_extender_1
  assign bit_extender_2_out = {{16{S[15]}}, S[15:0]};  // Bit_Extender bit_extender_2
  assign bit_extender_3_out = {{24{1'b0}}, S[7:0]};  // Bit_Extender bit_extender_3
  assign bit_extender_4_out = {{16{1'b0}}, S[15:0]};  // Bit_Extender bit_extender_4
  Multiplexer #(.width(32), .select(3), .enable("false")) multiplexer_1 (
    .in0(bit_extender_1_out), .in1(bit_extender_2_out), .in2(Word), .in3(Word), .in4(bit_extender_3_out),
    .in5(bit_extender_4_out), .in6(Word), .in7(Word), .out(Data), .sel(funct3));

  // Other names for the same wires on the sheet: sh[4:3] = Off

  // Notes on the sheet:
  //   Load Unit: lay byte/halfword tu word doc ra va mo rong dau (sign) hoac them 0 (zero)
  //   Word >> (Off*8) dua byte can lay ve vi tri thap nhat;  funct3 chon: 000 LB, 001 LH, 010 LW, 100 LBU, 101 LHU
  //   sh = Off * 8 = {Off,000}
  //   LB: sign-extend S[7:0]
  //   LH: sign-extend S[15:0]
  //   LBU: zero-extend S[7:0]
  //   LHU: zero-extend S[15:0]
  //   funct3 = 010 (LW): Word
endmodule

module PerfCounters (
  input  CLK,
  input  Run,
  input  Retire,
  output [31:0] cycles,
  output [31:0] instret
);

  wire en_i;
  wire [31:0] adder_1_out, adder_2_out;

  and and_1 (en_i, Run, Retire);
  Adder #(.width(32)) adder_1 (.a(cycles), .b(32'h1), .out(adder_1_out), .cin(1'b0));  // open: cout
  Adder #(.width(32)) adder_2 (.a(instret), .b(32'h1), .out(adder_2_out), .cin(1'b0));  // open: cout
  Register #(.width(32)) u_cycles (.D(adder_1_out), .en(Run), .clk(CLK), .Q(cycles), .clr(1'b0));
  Register #(.width(32)) u_instret (.D(adder_2_out), .en(en_i), .clk(CLK), .Q(instret), .clr(1'b0));

  // Notes on the sheet:
  //   Performance counters: cycles dem moi canh len CLK khi CPU dang chay (Run=1),
  //   instret dem so lenh da hoan thanh (Retire=1).  CPI = cycles / instret
endmodule

module IOController (
  input  [31:0] Addr,
  input  [31:0] WData,
  input  MemWrite,
  input  MemRead,
  input  IsIO,
  input  CLK,
  input  [6:0] KbdData,
  input  KbdAvail,
  input  [7:0] GpioIn,
  output [31:0] IoRData,
  output TxWE,
  output [6:0] TxData,
  output KbdRE,
  output [31:0] GpioOut
);

  wire gpioWE, selGPIO, selRX, selTX;
  wire [31:0] r_gpioin, r_rx;

  Decoder #(.select(3), .enable("true")) decoder_1 (
    .out0(selTX), .out1(selRX), .out4(selGPIO), .sel(Addr[4:2]), .en(IsIO));  // open: out2, out3, out5, out6, out7
  and and_1 (TxWE, MemWrite, selTX);
  and and_2 (KbdRE, MemRead, selRX);
  and and_3 (gpioWE, MemWrite, selGPIO);
  Register #(.width(32)) GPIO_OUT (.D(WData), .en(gpioWE), .clk(CLK), .Q(GpioOut), .clr(1'b0));
  assign r_rx = {{25{1'b0}}, KbdData};  // Bit_Extender bit_extender_1
  assign r_gpioin = {{24{1'b0}}, GpioIn};  // Bit_Extender bit_extender_2
  Multiplexer #(.width(32), .select(3), .enable("false")) multiplexer_1 (
    .in0({32{1'b0}}), .in1(r_rx), .in2({31'h1, KbdAvail}), .in3({32{1'b0}}), .in4(GpioOut), .in5(r_gpioin),
    .in6({32{1'b0}}), .in7({32{1'b0}}), .out(IoRData), .sel(Addr[4:2]));

  assign TxData = WData[6:0];

  // Other names for the same wires on the sheet: idx[2:0] = Addr[4:2]; r_status[0] = KbdAvail

  // Notes on the sheet:
  //   I/O Controller (memory-mapped I/O): thiet bi ngoai vi chi la vai dia chi dac biet
  //   Vung I/O: Addr[31:28] = 0xF.  Thanh ghi I/O chon bang Addr[4:2]:
  //   0xF0000000 UART_TXDATA (W)   0xF0000004 UART_RXDATA (R)   0xF0000008 UART_STATUS (R)
  //   0xF0000010 GPIO_OUT (R/W)    0xF0000014 GPIO_IN (R)       dia chi khac trong vung: doc = 0
  //   Doc RXDATA lay ky tu ra khoi hang doi -> chi bat KbdRE khi la LENH LOAD that (MemRead=1)
  //   idx = Addr[4:2]
  //   chon thanh ghi I/O
  //   STATUS = {0..., 1, KbdAvail}
  //   doc I/O theo idx
endmodule
