// Logisim project RV32I_Pipeline_NoHazard.circ as structural Verilog: 19 circuits, main circuit RV32I_Pipeline_NoHazard
module RV32I_Pipeline_NoHazard (
  output halt,
  output [31:0] cycles,
  output [31:0] instret,
  output [31:0] pc,
  output [31:0] gpio
);

  wire branchunit_1_taken, CLK, D_Branch, D_BSel, D_f7b5, D_Halt, D_Jal, D_Jalr, D_MemRead, D_MemWrite,
       D_RegWrite, D_UseRs1, D_UseRs2, D_valid, E_Branch, E_BSel, E_Halt, E_isLink, E_Jal, E_Jalr, E_MemRead,
       E_MemToReg, E_MemWrite, E_Redirect, E_RegWrite, E_valid, IDEX_Flush, IFID_Flush, IFID_Write,
       IO_kbdavail, IO_kbdre, IO_txwe, LoadUse, M_Halt, M_IsIO, M_MemRead, M_MemToReg, M_MemWrite, M_RamWE,
       M_RegWrite, M_valid, PCWrite, Run, Stall, W_MemToReg, W_RegWrite, W_valid;
  wire [1:0] D_ALUOp, D_ASel, D_WBSel, E_ASel, FwdA, FwdB, M_Off;
  wire [2:0] D_funct3, D_ImmSel, E_funct3, M_funct3;
  wire [3:0] D_ALUCtrl, E_ALUCtrl;
  wire [4:0] D_rd, D_rs1, D_rs2, E_rd, E_rs1, E_rs2, M_rd, W_rd;
  wire [6:0] IO_kbddata, IO_txdata;
  wire [7:0] IO_gpioin;
  wire [11:0] M_WordAddr;
  wire [31:0] D_imm, D_instr, D_pc, D_pc4, D_rs1d, D_rs2d, E_alu, E_exres, E_fa, E_fb, E_imm, E_instr, E_pc,
       E_pc4, E_rs1d, E_rs2d, E_target, F_instr, F_pc4, IO_rdata, M_exres, M_instr, M_mdata, M_memword, M_pc,
       M_ramout, M_sdata, M_stnew, multiplexer_1_out, multiplexer_4_out, multiplexer_5_out,
       registerfile_1_rd1, registerfile_1_rd2, W_data, W_exres, W_instr, W_mdata, W_pc;

  Clock u_CLK (.out(CLK));
  Multiplexer #(.width(32), .select(1), .enable("false")) multiplexer_1 (
    .in0(F_pc4), .in1(E_target), .out(multiplexer_1_out), .sel(E_Redirect));
  Register #(.width(32)) u_PC (.D(multiplexer_1_out), .en(PCWrite), .clk(CLK), .Q(pc), .clr(1'b0));
  not not_1 (Run, halt);
  // Probe on pc
  // Probe on F_instr
  // Probe on Stall
  Adder #(.width(32)) adder_1 (.a(pc), .b(32'h4), .out(F_pc4), .cin(1'b0));  // open: cout
  ROM #(.addrWidth(10), .dataWidth(32)) IMEM (.addr(pc[11:2]), .data(F_instr));
  PerfCounters perfcounters_1 (.CLK(CLK), .Run(Run), .Retire(W_valid), .cycles(cycles), .instret(instret));
  // Probe on D_pc
  // Probe on D_instr
  // Probe on LoadUse
  IF_ID if_id_1 (
    .D_valid(1'b1), .D_pc(pc), .D_pc4(F_pc4), .D_instr(F_instr), .Q_valid(D_valid), .Q_pc(D_pc),
    .Q_pc4(D_pc4), .Q_instr(D_instr), .CLK(CLK), .EN(IFID_Write), .FLUSH(IFID_Flush));
  // Probe on E_pc
  // Probe on E_instr
  // Probe on E_Redirect
  Control control_1 (
    .Instr(D_instr), .rd(D_rd), .rs1(D_rs1), .rs2(D_rs2), .funct3(D_funct3), .f7b5(D_f7b5),
    .RegWrite(D_RegWrite), .ASel(D_ASel), .BSel(D_BSel), .ALUOp(D_ALUOp), .ImmSel(D_ImmSel),
    .MemRead(D_MemRead), .MemWrite(D_MemWrite), .WBSel(D_WBSel), .Branch(D_Branch), .Jal(D_Jal),
    .Jalr(D_Jalr), .Halt(D_Halt), .UseRs1(D_UseRs1), .UseRs2(D_UseRs2));
  // Probe on M_pc
  // Probe on M_instr
  // Probe on FwdA
  RegisterFile registerfile_1 (
    .RA1(D_rs1), .RA2(D_rs2), .WA(W_rd), .WD(W_data), .WE(W_RegWrite), .CLK(CLK), .RD1(registerfile_1_rd1),
    .RD2(registerfile_1_rd2));
  ImmGen immgen_1 (.Instr(D_instr), .ImmSel(D_ImmSel), .Imm(D_imm));
  ALUControl alucontrol_1 (.ALUOp(D_ALUOp), .funct3(D_funct3), .f7b5(D_f7b5), .ALUCtrl(D_ALUCtrl));
  // Probe on W_pc
  // Probe on W_instr
  // Probe on FwdB
  HazardUnit hazardunit_1 (
    .rs1(D_rs1), .rs2(D_rs2), .UseRs1(D_UseRs1), .UseRs2(D_UseRs2), .D_Halt(D_Halt), .E_rd(E_rd),
    .E_MemRead(1'b0), .Redirect(E_Redirect), .PCWrite(PCWrite), .IFID_Write(IFID_Write),
    .IFID_Flush(IFID_Flush), .IDEX_Flush(IDEX_Flush), .Stall(Stall), .LoadUse(LoadUse));
  IDBypass idbypass_1 (
    .RD1(registerfile_1_rd1), .RD2(registerfile_1_rd2), .rs1(D_rs1), .rs2(D_rs2), .W_rd(W_rd),
    .W_RegWrite(W_RegWrite), .W_data(W_data), .O1(D_rs1d), .O2(D_rs2d));
  ID_EX id_ex_1 (
    .D_valid(D_valid), .D_pc(D_pc), .D_pc4(D_pc4), .D_instr(D_instr), .D_rs1d(D_rs1d), .D_rs2d(D_rs2d),
    .D_imm(D_imm), .D_rs1(D_rs1), .D_rs2(D_rs2), .D_rd(D_rd), .D_funct3(D_funct3), .D_ALUCtrl(D_ALUCtrl),
    .D_ASel(D_ASel), .D_BSel(D_BSel), .D_RegWrite(D_RegWrite), .D_MemRead(D_MemRead),
    .D_MemWrite(D_MemWrite), .D_WBSel(D_WBSel), .D_Branch(D_Branch), .D_Jal(D_Jal), .D_Jalr(D_Jalr),
    .D_Halt(D_Halt), .Q_valid(E_valid), .Q_pc(E_pc), .Q_pc4(E_pc4), .Q_instr(E_instr), .Q_rs1d(E_rs1d),
    .Q_rs2d(E_rs2d), .Q_imm(E_imm), .Q_rs1(E_rs1), .Q_rs2(E_rs2), .Q_rd(E_rd), .Q_funct3(E_funct3),
    .Q_ALUCtrl(E_ALUCtrl), .Q_ASel(E_ASel), .Q_BSel(E_BSel), .Q_RegWrite(E_RegWrite), .Q_MemRead(E_MemRead),
    .Q_MemWrite(E_MemWrite), .Q_WBSel({E_isLink, E_MemToReg}), .Q_Branch(E_Branch), .Q_Jal(E_Jal),
    .Q_Jalr(E_Jalr), .Q_Halt(E_Halt), .CLK(CLK), .EN(1'b1), .FLUSH(IDEX_Flush));
  Multiplexer #(.width(32), .select(2), .enable("false")) multiplexer_2 (
    .in0(E_rs1d), .in1(M_exres), .in2(W_data), .in3({32{1'b0}}), .out(E_fa), .sel(2'b00));
  Multiplexer #(.width(32), .select(2), .enable("false")) multiplexer_3 (
    .in0(E_rs2d), .in1(M_exres), .in2(W_data), .in3({32{1'b0}}), .out(E_fb), .sel(2'b00));
  ForwardUnit forwardunit_1 (
    .rs1(E_rs1), .rs2(E_rs2), .M_rd(M_rd), .M_RegWrite(M_RegWrite), .W_rd(W_rd), .W_RegWrite(W_RegWrite),
    .FwdA(FwdA), .FwdB(FwdB));
  Multiplexer #(.width(32), .select(2), .enable("false")) multiplexer_4 (
    .in0(E_fa), .in1(E_pc), .in2({32{1'b0}}), .in3({32{1'b0}}), .out(multiplexer_4_out), .sel(E_ASel));
  Multiplexer #(.width(32), .select(1), .enable("false")) multiplexer_5 (
    .in0(E_fb), .in1(E_imm), .out(multiplexer_5_out), .sel(E_BSel));
  ALU alu_1 (.A(multiplexer_4_out), .B(multiplexer_5_out), .Y(E_alu), .ALUCtrl(E_ALUCtrl));
  BranchUnit branchunit_1 (.A(E_fa), .B(E_fb), .funct3(E_funct3), .Branch(E_Branch), .Taken(branchunit_1_taken));
  // Probe on E_alu
  assign E_target = E_alu & 32'hfffffffe;  // AND_Gate and_1, 32 bits wide
  or or_1 (E_Redirect, E_Jal, E_Jalr, branchunit_1_taken);
  Multiplexer #(.width(32), .select(1), .enable("false")) multiplexer_6 (
    .in0(E_alu), .in1(E_pc4), .out(E_exres), .sel(E_isLink));
  EX_MEM ex_mem_1 (
    .D_valid(E_valid), .D_pc(E_pc), .D_instr(E_instr), .D_exres(E_exres), .D_sdata(E_fb), .D_rd(E_rd),
    .D_funct3(E_funct3), .D_RegWrite(E_RegWrite), .D_MemRead(E_MemRead), .D_MemWrite(E_MemWrite),
    .D_MemToReg(E_MemToReg), .D_Halt(E_Halt), .Q_valid(M_valid), .Q_pc(M_pc), .Q_instr(M_instr),
    .Q_exres(M_exres), .Q_sdata(M_sdata), .Q_rd(M_rd), .Q_funct3(M_funct3), .Q_RegWrite(M_RegWrite),
    .Q_MemRead(M_MemRead), .Q_MemWrite(M_MemWrite), .Q_MemToReg(M_MemToReg), .Q_Halt(M_Halt), .CLK(CLK),
    .EN(1'b1), .FLUSH(1'b0));
  StoreUnit storeunit_1 (.Old(M_memword), .WData(M_sdata), .Off(M_Off), .funct3(M_funct3), .New(M_stnew));
  IOController iocontroller_1 (
    .Addr(M_exres), .WData(M_stnew), .MemWrite(M_MemWrite), .MemRead(M_MemRead), .IsIO(M_IsIO), .CLK(CLK),
    .KbdData(IO_kbddata), .KbdAvail(IO_kbdavail), .GpioIn(IO_gpioin), .IoRData(IO_rdata), .TxWE(IO_txwe),
    .TxData(IO_txdata), .KbdRE(IO_kbdre), .GpioOut(gpio));
  DipSwitch #(.number(8)) dipswitch_1 (
    .sw1(IO_gpioin[7]), .sw2(IO_gpioin[6]), .sw3(IO_gpioin[5]), .sw4(IO_gpioin[4]), .sw5(IO_gpioin[3]),
    .sw6(IO_gpioin[2]), .sw7(IO_gpioin[1]), .sw8(IO_gpioin[0]));
  AddrDecode addrdecode_1 (
    .Addr(M_exres), .MemWrite(M_MemWrite), .WordAddr(M_WordAddr), .Off(M_Off), .RamWE(M_RamWE), .IsIO(M_IsIO));  // open: IoWE
  RAM #(.addrWidth(12), .dataWidth(32), .asyncread("true"), .databus("bibus")) DMEM (
    .addr(M_WordAddr), .we(M_RamWE), .oe(1'b1), .clk(CLK), .din(M_stnew), .dout(M_ramout));
  LoadUnit loadunit_1 (.Word(M_memword), .Off(M_Off), .funct3(M_funct3), .Data(M_mdata));
  Multiplexer #(.width(32), .select(1), .enable("false")) multiplexer_7 (
    .in0(M_ramout), .in1(IO_rdata), .out(M_memword), .sel(M_IsIO));
  TTY #(.rows(8), .cols(32)) tty_1 (.data(IO_txdata), .clk(CLK), .we(IO_txwe), .clr(1'b0));
  Keyboard #(.buflen(32)) keyboard_1 (.clk(CLK), .re(IO_kbdre), .clr(1'b0), .avail(IO_kbdavail), .data(IO_kbddata));
  MEM_WB mem_wb_1 (
    .D_valid(M_valid), .D_pc(M_pc), .D_instr(M_instr), .D_exres(M_exres), .D_mdata(M_mdata), .D_rd(M_rd),
    .D_RegWrite(M_RegWrite), .D_MemToReg(M_MemToReg), .D_Halt(M_Halt), .Q_valid(W_valid), .Q_pc(W_pc),
    .Q_instr(W_instr), .Q_exres(W_exres), .Q_mdata(W_mdata), .Q_rd(W_rd), .Q_RegWrite(W_RegWrite),
    .Q_MemToReg(W_MemToReg), .Q_Halt(halt), .CLK(CLK), .EN(1'b1), .FLUSH(1'b0));
  Hex_Digit_Display #(.decimalPoint("false")) hex_digit_display_1 (.value(gpio[15:12]));
  Multiplexer #(.width(32), .select(1), .enable("false")) multiplexer_8 (
    .in0(W_exres), .in1(W_mdata), .out(W_data), .sel(W_MemToReg));
  // Probe on W_data
  Hex_Digit_Display #(.decimalPoint("false")) hex_digit_display_2 (.value(gpio[11:8]));
  Hex_Digit_Display #(.decimalPoint("false")) hex_digit_display_3 (.value(gpio[7:4]));
  // LedBar #(.matrixcols(8), .inputtype("row")) ledbar_1: pin names not known; wires that end beside it: gpio[23:16]
  Hex_Digit_Display #(.decimalPoint("false")) hex_digit_display_4 (.value(gpio[3:0]));

  // Other names for the same wires on the sheet: E_WBSel[1:0] = {E_isLink, E_MemToReg}; F_pc[31:0] = pc;
  //   IO_gpio[31:0] = gpio; IO_hex3[3:0] = gpio[3:0]; IO_hex2[3:0] = gpio[7:4]; IO_hex1[3:0] = gpio[11:8];
  //   IO_hex0[3:0] = gpio[15:12]; IO_led[7:0] = gpio[23:16]; W_Halt = halt

  // Notes on the sheet:
  //   RV32I 5-STAGE PIPELINE CPU   IF -> ID -> EX -> MEM -> WB
  //   Data hazard: Forwarding (EX/MEM->EX, MEM/WB->EX) + WB->ID bypass + Load-use stall 1 chu ky
  //   Control hazard: du doan "khong nhay"; branch/JAL/JALR giai quyet o EX -> neu nhay thi flush 2 lenh (IF/ID, ID/EX)
  //   Ten tunnel: F_ = Fetch, D_ = Decode, E_ = Execute, M_ = Memory, W_ = Writeback (gia tri dang o tang do)
  //   Chay: Ctrl+K (auto tick) / Ctrl+T (1 nua chu ky).  Nap chuong trinh: chuot phai ROM IMEM > Load Image
  //   next PC
  //   PIPELINE MONITOR (PC va ma lenh o tung tang; instr = 00000000 la bubble)
  //   IF
  //   IF
  //   PC[11:2]
  //   contents of IMEM (hex, n*v repeats v):
  //   4137 13 13 ff010113 437 13 13 40413 293 100313 c00393 542023 628e33 30293 13 e0313 440413 fff38393
  //   13 13 fc039ee3 437 13 13 40413 513 c00393 42e83 13 13 1d50533 440413 fff38393 13 13 fe0390e3
  //   f00004b7 13 13 48493 4800f13 13 13 1e48023 6500f13 13 13 1e48023 6c00f13 13 13 1e48023 6c00f13 13 13
  //   1e48023 6f00f13 13 13 1e48023 2000f13 13 13 1e48023 5200f13 13 13 1e48023 4900f13 13 13 1e48023
  //   5300f13 13 13 1e48023 4300f13 13 13 1e48023 2d00f13 13 13 1e48023 5600f13 13 13 1e48023 2100f13 13
  //   13 1e48023 a00f13 13 13 1e48023 a4a823 ff00f13 13 13 1e48923 100073
  //   ID
  //   EX
  //   MEM
  //   ID
  //   WB
  //   Fwd: 0 ID/EX, 1 EX/MEM, 2 MEM/WB
  //   EX
  //   ASel
  //   BSel
  //   Redirect = Taken|Jal|Jalr ; target = ALU & ~1
  //   exres = (JAL/JALR) ? PC+4 : ALU
  //   MEM
  //   GPIO_IN: 8 DIP switch (0xF0000014), trai = bit 7
  //   IsIO ? I/O : RAM
  //   UART TX: TTY  (0xF0000000)
  //   UART RX: Keyboard (0xF0000004)
  //   STATUS 0xF0000008. Click vao Keyboard roi go phim
  //   WB
  //   GPIO_OUT (0xF0000010): [15:0] hex, [23:16] LED
endmodule

module Control (
  input  [31:0] Instr,
  output [4:0] rd,
  output [4:0] rs1,
  output [4:0] rs2,
  output [2:0] funct3,
  output f7b5,
  output RegWrite,
  output [1:0] ASel,
  output BSel,
  output [1:0] ALUOp,
  output [2:0] ImmSel,
  output MemRead,
  output MemWrite,
  output [1:0] WBSel,
  output Branch,
  output Jal,
  output Jalr,
  output Halt,
  output UseRs1,
  output UseRs2
);

  wire decoder_1_out5, decoder_1_out12, valid;

  and and_1 (valid, Instr[0], Instr[1]);
  Decoder #(.select(5), .enable("true")) decoder_1 (
    .out0(MemRead), .out4(ALUOp[0]), .out5(decoder_1_out5), .out8(MemWrite), .out12(decoder_1_out12),
    .out13(ASel[1]), .out24(Branch), .out25(Jalr), .out27(ImmSel[2]), .out28(Halt), .sel(Instr[6:2]),
    .en(valid));  // open: out1, out2, out3, out6, out7, out9, out10, out11, out14, out15, out16, out17, out18, out19, out20, out21, out22, out23, out26, out29, out30, out31
  or or_1 (RegWrite, decoder_1_out12, ALUOp[0], MemRead, ImmSel[2], Jalr, ASel[1], decoder_1_out5);
  or or_2 (ASel[0], Branch, ImmSel[2], decoder_1_out5);
  or or_3 (BSel, ALUOp[0], MemRead, MemWrite, Branch, ImmSel[2], Jalr, ASel[1], decoder_1_out5);
  or or_4 (ALUOp[1], decoder_1_out12, ALUOp[0]);
  or or_5 (ImmSel[0], MemWrite, ASel[1], decoder_1_out5);
  or or_6 (ImmSel[1], Branch, ASel[1], decoder_1_out5);
  or or_7 (WBSel[1], ImmSel[2], Jalr);
  or or_8 (UseRs1, decoder_1_out12, ALUOp[0], MemRead, MemWrite, Branch, Jalr);
  or or_9 (UseRs2, decoder_1_out12, MemWrite, Branch);

  assign f7b5 = Instr[30];
  assign funct3 = Instr[14:12];
  assign Jal = ImmSel[2];
  assign rd = Instr[11:7];
  assign rs1 = Instr[19:15];
  assign rs2 = Instr[24:20];
  assign WBSel[0] = MemRead;

  // Other names for the same wires on the sheet: q0 = Instr[0]; q1 = Instr[1]; opc[4:0] = Instr[6:2];
  //   WBSel0 = MemRead

  // Notes on the sheet:
  //   Control Unit (Main Decoder) - ve theo kieu PLA:
  //   1) Decoder 5->32 bien opcode[6:2] thanh 1 duong "one-hot" cho moi nhom lenh (chi bat khi opcode[1:0]=11)
  //   2) Moi tin hieu dieu khien = OR cua cac nhom lenh can no (cot doc = nhom lenh, cham tron = co noi)
  //   Lenh = 0x00000000 (bubble) -> opcode[1:0]=00 -> decoder tat -> moi tin hieu = 0 = NOP
  //   tach truong lenh
  //   valid = opcode[1:0]==11
  //   opcode[6:2]
  //   JAL
  //   SYSTEM
  //   BRANCH
  //   JALR
  //   OP
  //   LUI
  //   AUIPC
  //   STORE
  //   LOAD
  //   OPIMM
  //   Bang chan ly (1 = bat):
  //   nhom     opcode  RegW ASel BSel ALUOp ImmSel MemR MemW WBSel
  //   OP       0110011  1    00   0    10    -      0    0    00
  //   OP-IMM   0010011  1    00   1    11    I      0    0    00
  //   LOAD     0000011  1    00   1    00    I      1    0    01
  //   STORE    0100011  0    00   1    00    S      0    1    --
  //   BRANCH   1100011  0    01   1    00    B      0    0    --
  //   JAL      1101111  1    01   1    00    J      0    0    10
  //   JALR     1100111  1    00   1    00    I      0    0    10
  //   LUI      0110111  1    10   1    00    U      0    0    00
  //   AUIPC    0010111  1    01   1    00    U      0    0    00
  //   SYSTEM   1110011  0  (Halt = 1: ECALL/EBREAK dung CPU)
  //   ASel: 0=rs1 1=PC 2=0   WBSel: 0=ALU 1=Mem 2=PC+4
  //   ImmSel: 0=I 1=S 2=B 3=U 4=J
endmodule

module RegisterFile (
  input  [4:0] RA1,
  input  [4:0] RA2,
  input  [4:0] WA,
  input  [31:0] WD,
  input  WE,
  input  CLK,
  output [31:0] RD1,
  output [31:0] RD2
);

  wire we1, we2, we3, we4, we5, we6, we7, we8, we9, we10, we11, we12, we13, we14, we15, we16, we17, we18,
       we19, we20, we21, we22, we23, we24, we25, we26, we27, we28, we29, we30, we31;
  wire [31:0] x1, x2, x3, x4, x5, x6, x7, x8, x9, x10, x11, x12, x13, x14, x15, x16, x17, x18, x19, x20, x21,
       x22, x23, x24, x25, x26, x27, x28, x29, x30, x31;

  Decoder #(.select(5), .enable("true")) decoder_1 (
    .out1(we1), .out2(we2), .out3(we3), .out4(we4), .out5(we5), .out6(we6), .out7(we7), .out8(we8),
    .out9(we9), .out10(we10), .out11(we11), .out12(we12), .out13(we13), .out14(we14), .out15(we15),
    .out16(we16), .out17(we17), .out18(we18), .out19(we19), .out20(we20), .out21(we21), .out22(we22),
    .out23(we23), .out24(we24), .out25(we25), .out26(we26), .out27(we27), .out28(we28), .out29(we29),
    .out30(we30), .out31(we31), .sel(WA), .en(WE));  // open: out0
  Register #(.width(32)) x1_ra (.D(WD), .en(we1), .clk(CLK), .Q(x1), .clr(1'b0));
  Register #(.width(32)) x2_sp (.D(WD), .en(we2), .clk(CLK), .Q(x2), .clr(1'b0));
  Register #(.width(32)) x3_gp (.D(WD), .en(we3), .clk(CLK), .Q(x3), .clr(1'b0));
  Register #(.width(32)) x4_tp (.D(WD), .en(we4), .clk(CLK), .Q(x4), .clr(1'b0));
  Register #(.width(32)) x5_t0 (.D(WD), .en(we5), .clk(CLK), .Q(x5), .clr(1'b0));
  Register #(.width(32)) x6_t1 (.D(WD), .en(we6), .clk(CLK), .Q(x6), .clr(1'b0));
  Register #(.width(32)) x7_t2 (.D(WD), .en(we7), .clk(CLK), .Q(x7), .clr(1'b0));
  Register #(.width(32)) x8_s0 (.D(WD), .en(we8), .clk(CLK), .Q(x8), .clr(1'b0));
  Register #(.width(32)) x9_s1 (.D(WD), .en(we9), .clk(CLK), .Q(x9), .clr(1'b0));
  Register #(.width(32)) x10_a0 (.D(WD), .en(we10), .clk(CLK), .Q(x10), .clr(1'b0));
  Register #(.width(32)) x11_a1 (.D(WD), .en(we11), .clk(CLK), .Q(x11), .clr(1'b0));
  Register #(.width(32)) x12_a2 (.D(WD), .en(we12), .clk(CLK), .Q(x12), .clr(1'b0));
  Register #(.width(32)) x13_a3 (.D(WD), .en(we13), .clk(CLK), .Q(x13), .clr(1'b0));
  Register #(.width(32)) x14_a4 (.D(WD), .en(we14), .clk(CLK), .Q(x14), .clr(1'b0));
  Register #(.width(32)) x15_a5 (.D(WD), .en(we15), .clk(CLK), .Q(x15), .clr(1'b0));
  Register #(.width(32)) x16_a6 (.D(WD), .en(we16), .clk(CLK), .Q(x16), .clr(1'b0));
  Register #(.width(32)) x17_a7 (.D(WD), .en(we17), .clk(CLK), .Q(x17), .clr(1'b0));
  Register #(.width(32)) x18_s2 (.D(WD), .en(we18), .clk(CLK), .Q(x18), .clr(1'b0));
  Register #(.width(32)) x19_s3 (.D(WD), .en(we19), .clk(CLK), .Q(x19), .clr(1'b0));
  Register #(.width(32)) x20_s4 (.D(WD), .en(we20), .clk(CLK), .Q(x20), .clr(1'b0));
  Register #(.width(32)) x21_s5 (.D(WD), .en(we21), .clk(CLK), .Q(x21), .clr(1'b0));
  Register #(.width(32)) x22_s6 (.D(WD), .en(we22), .clk(CLK), .Q(x22), .clr(1'b0));
  Register #(.width(32)) x23_s7 (.D(WD), .en(we23), .clk(CLK), .Q(x23), .clr(1'b0));
  Register #(.width(32)) x24_s8 (.D(WD), .en(we24), .clk(CLK), .Q(x24), .clr(1'b0));
  Register #(.width(32)) x25_s9 (.D(WD), .en(we25), .clk(CLK), .Q(x25), .clr(1'b0));
  Register #(.width(32)) x26_s10 (.D(WD), .en(we26), .clk(CLK), .Q(x26), .clr(1'b0));
  Register #(.width(32)) x27_s11 (.D(WD), .en(we27), .clk(CLK), .Q(x27), .clr(1'b0));
  Register #(.width(32)) x28_t3 (.D(WD), .en(we28), .clk(CLK), .Q(x28), .clr(1'b0));
  Register #(.width(32)) x29_t4 (.D(WD), .en(we29), .clk(CLK), .Q(x29), .clr(1'b0));
  Register #(.width(32)) x30_t5 (.D(WD), .en(we30), .clk(CLK), .Q(x30), .clr(1'b0));
  Register #(.width(32)) x31_t6 (.D(WD), .en(we31), .clk(CLK), .Q(x31), .clr(1'b0));
  Multiplexer #(.width(32), .select(5), .enable("false")) multiplexer_1 (
    .in0({32{1'b0}}), .in1(x1), .in2(x2), .in3(x3), .in4(x4), .in5(x5), .in6(x6), .in7(x7), .in8(x8),
    .in9(x9), .in10(x10), .in11(x11), .in12(x12), .in13(x13), .in14(x14), .in15(x15), .in16(x16), .in17(x17),
    .in18(x18), .in19(x19), .in20(x20), .in21(x21), .in22(x22), .in23(x23), .in24(x24), .in25(x25),
    .in26(x26), .in27(x27), .in28(x28), .in29(x29), .in30(x30), .in31(x31), .out(RD1), .sel(RA1));
  Multiplexer #(.width(32), .select(5), .enable("false")) multiplexer_2 (
    .in0({32{1'b0}}), .in1(x1), .in2(x2), .in3(x3), .in4(x4), .in5(x5), .in6(x6), .in7(x7), .in8(x8),
    .in9(x9), .in10(x10), .in11(x11), .in12(x12), .in13(x13), .in14(x14), .in15(x15), .in16(x16), .in17(x17),
    .in18(x18), .in19(x19), .in20(x20), .in21(x21), .in22(x22), .in23(x23), .in24(x24), .in25(x25),
    .in26(x26), .in27(x27), .in28(x28), .in29(x29), .in30(x30), .in31(x31), .out(RD2), .sel(RA2));

  // Notes on the sheet:
  //   Register File 32 x 32-bit: 2 cong doc (to hop, khong can clock) + 1 cong ghi (canh len CLK)
  //   Ghi: Decoder 5->32 bien WA thanh one-hot, AND voi WE -> chi 1 thanh ghi duoc bat Enable
  //   Doc: 2 MUX 32->1 chon theo RA1/RA2.  x0 khong phai thanh ghi: dau vao 0 cua MUX noi hang so 0
  //   write decoder
  //   x0 (zero)
  //   khong luu tru:
  //   doc luon = 0
  //   read port 1
  //   read port 2
endmodule

module ImmGen (
  input  [31:0] Instr,
  input  [2:0] ImmSel,
  output [31:0] Imm
);

  wire [31:0] bit_extender_1_out, bit_extender_2_out, bit_extender_3_out, bit_extender_4_out;

  assign bit_extender_1_out = {{20{Instr[31]}}, Instr[31:20]};  // Bit_Extender bit_extender_1
  assign bit_extender_2_out = {{20{Instr[31]}}, {Instr[31:25], Instr[11:7]}};  // Bit_Extender bit_extender_2
  assign bit_extender_3_out = {{19{Instr[31]}}, {Instr[31], Instr[7], Instr[30:25], Instr[11:8], 1'b0}};  // Bit_Extender bit_extender_3
  assign bit_extender_4_out = {{11{Instr[31]}}, {Instr[31], Instr[19:12], Instr[20], Instr[30:21], 1'b0}};  // Bit_Extender bit_extender_4
  Multiplexer #(.width(32), .select(3), .enable("false")) multiplexer_1 (
    .in0(bit_extender_1_out), .in1(bit_extender_2_out), .in2(bit_extender_3_out),
    .in3({Instr[31:12], {12{1'b0}}}), .in4(bit_extender_4_out), .in5({32{1'b0}}), .in6({32{1'b0}}),
    .in7({32{1'b0}}), .out(Imm), .sel(ImmSel));

  // Other names for the same wires on the sheet: i11_8[3:0] = Instr[11:8]; i7 = Instr[7]; i24_21[3:0] = Instr[24:21];
  //   i30_25[5:0] = Instr[30:25]; i20 = Instr[20]; i14_12[2:0] = Instr[14:12]; i19_15[4:0] = Instr[19:15];
  //   i31 = Instr[31]

  // Notes on the sheet:
  //   Immediate Generator: ghep cac manh bit cua lenh thanh hang so 32-bit (sign-extend)
  //   RISC-V co tinh "xao tron" bit cua B/J-type de bit dau (inst[31]) luon la bit dau cua imm
  //   va cac manh bit nam o cung vi tri giua cac dang lenh -> phan cung chi can noi day + MUX.
  //   ImmSel: 0=I  1=S  2=B  3=U  4=J
  //   inst[7]
  //   inst[11:8]
  //   inst[14:12]
  //   inst[19:15]
  //   inst[20]
  //   inst[24:21]
  //   inst[30:25]
  //   inst[31]
  //   I-type  imm[11:0]
  //   S-type  imm[11:0]
  //   B-type  imm[12:0]
  //   U-type  imm[31:0]
  //   J-type  imm[20:0]
  //   ImmSel: 0=I 1=S 2=B 3=U 4=J
endmodule

module ALUControl (
  input  [1:0] ALUOp,
  input  [2:0] funct3,
  input  f7b5,
  output [3:0] ALUCtrl
);

  wire comparator_1_eq, or_1_out;

  Multiplexer #(.width(3), .select(1), .enable("false")) multiplexer_1 (
    .in0(3'b000), .in1(funct3), .out(ALUCtrl[2:0]), .sel(ALUOp[1]));
  Comparator #(.width(3), .mode("unsigned")) comparator_1 (
    .a(funct3), .b(3'b101), .eq(comparator_1_eq));  // open: gt, lt
  or or_1 (or_1_out, ~ALUOp[0], comparator_1_eq);  // OR_Gate
  and and_1 (ALUCtrl[3], ALUOp[1], f7b5, or_1_out);

  // Other names for the same wires on the sheet: op[2:0] = ALUCtrl[2:0]; alt = ALUCtrl[3]

  // Notes on the sheet:
  //   ALU Control: (ALUOp, funct3, bit30) -> ALUCtrl[3:0] = {alt, op}
  //   ALUOp 00: ADD (load/store/branch/jump/lui/auipc)   10: R-type   11: I-type
  //   R-type: alt = bit30 (SUB/SRA).  I-type: alt = bit30 CHI KHI funct3=101 (SRAI);
  //   voi ADDI bit30 la mot phan cua immediate nen phai bo qua (khong co SUBI).
  //   op = ALUOp[1] ? funct3 : 000
  //   funct3 == 101 ?
endmodule

module ALU (
  input  [31:0] A,
  input  [31:0] B,
  input  [3:0] ALUCtrl,
  output [31:0] Y
);

  wire comparator_1_lt, comparator_2_lt;
  wire [31:0] adder_1_out, and_1_out, bit_extender_1_out, bit_extender_2_out, multiplexer_1_out,
       multiplexer_2_out, or_1_out, shifter_1_out, shifter_2_out, shifter_3_out, subtractor_1_out, xor_1_out;

  Adder #(.width(32)) adder_1 (.a(A), .b(B), .out(adder_1_out), .cin(1'b0));  // open: cout
  Subtractor #(.width(32)) subtractor_1 (.a(A), .b(B), .out(subtractor_1_out), .bin(1'b0));  // open: bout
  Comparator #(.width(32), .mode("twosComplement")) comparator_1 (.a(A), .b(B), .lt(comparator_1_lt));  // open: gt, eq
  assign bit_extender_1_out = {{31{1'b0}}, comparator_1_lt};  // Bit_Extender bit_extender_1
  Comparator #(.width(32), .mode("unsigned")) comparator_2 (.a(A), .b(B), .lt(comparator_2_lt));  // open: gt, eq
  assign bit_extender_2_out = {{31{1'b0}}, comparator_2_lt};  // Bit_Extender bit_extender_2
  assign xor_1_out = A ^ B;  // XOR_Gate xor_1, 32 bits wide
  assign or_1_out = A | B;  // OR_Gate or_1, 32 bits wide
  assign and_1_out = A & B;  // AND_Gate and_1, 32 bits wide
  Shifter #(.width(32), .shift("ll")) shifter_1 (.in(A), .\dist (B[4:0]), .out(shifter_1_out));
  Shifter #(.width(32), .shift("lr")) shifter_2 (.in(A), .\dist (B[4:0]), .out(shifter_2_out));
  Shifter #(.width(32), .shift("ar")) shifter_3 (.in(A), .\dist (B[4:0]), .out(shifter_3_out));
  Multiplexer #(.width(32), .select(1), .enable("false")) multiplexer_1 (
    .in0(adder_1_out), .in1(subtractor_1_out), .out(multiplexer_1_out), .sel(ALUCtrl[3]));
  Multiplexer #(.width(32), .select(1), .enable("false")) multiplexer_2 (
    .in0(shifter_2_out), .in1(shifter_3_out), .out(multiplexer_2_out), .sel(ALUCtrl[3]));
  Multiplexer #(.width(32), .select(3), .enable("false")) multiplexer_3 (
    .in0(multiplexer_1_out), .in1(shifter_1_out), .in2(bit_extender_1_out), .in3(bit_extender_2_out),
    .in4(xor_1_out), .in5(multiplexer_2_out), .in6(or_1_out), .in7(and_1_out), .out(Y), .sel(ALUCtrl[2:0]));

  // Other names for the same wires on the sheet: op[2:0] = ALUCtrl[2:0]; alt = ALUCtrl[3]; shamt[4:0] = B[4:0]

  // Notes on the sheet:
  //   ALU 32-bit  (Arithmetic Logic Unit)
  //   ALUCtrl = {bit30, funct3}: ma hoa trung voi funct3 cua RISC-V -> ALUControl gan nhu chi la "noi day"
  //   tach ALUCtrl
  //   shamt = B[4:0]
  //   ADD
  //   SUB
  //   SLT
  //   SLTU
  //   XOR
  //   OR
  //   AND
  //   SLL
  //   SRL
  //   SRA
  //   alt=0: ADD  alt=1: SUB
  //   alt=0: SRL  alt=1: SRA
  //   op=0 ADD/SUB
  //   op=1 SLL
  //   op=2 SLT
  //   op=3 SLTU
  //   op=4 XOR
  //   op=5 SRL/SRA
  //   op=6 OR
  //   op=7 AND
endmodule

module BranchUnit (
  input  [31:0] A,
  input  [31:0] B,
  input  [2:0] funct3,
  input  Branch,
  output Taken
);

  wire comparator_1_eq, comparator_2_lt, ltu, multiplexer_1_out, xor_1_out;

  Comparator #(.width(32), .mode("unsigned")) comparator_1 (.a(A), .b(B), .eq(comparator_1_eq), .lt(ltu));  // open: gt
  Comparator #(.width(32), .mode("twosComplement")) comparator_2 (.a(A), .b(B), .lt(comparator_2_lt));  // open: gt, eq
  Multiplexer #(.width(1), .select(2), .enable("false")) multiplexer_1 (
    .in0(comparator_1_eq), .in1(1'b0), .in2(comparator_2_lt), .in3(ltu), .out(multiplexer_1_out),
    .sel(funct3[2:1]));
  xor xor_1 (xor_1_out, multiplexer_1_out, funct3[0]);
  and and_1 (Taken, xor_1_out, Branch);

  // Other names for the same wires on the sheet: inv = funct3[0]; kind[1:0] = funct3[2:1]

  // Notes on the sheet:
  //   Branch Unit: quyet dinh re nhanh (BEQ BNE BLT BGE BLTU BGEU)
  //   funct3[2:1] chon phep so sanh: 00 = (A==B), 10 = A<B co dau, 11 = A<B khong dau
  //   funct3[0] = 1 dao nguoc ket qua: BNE = !BEQ, BGE = !BLT, BGEU = !BLTU
  //   Taken = Branch AND cond
  //   unsigned
  //   signed (bu 2)
endmodule

module AddrDecode (
  input  [31:0] Addr,
  input  MemWrite,
  output [11:0] WordAddr,
  output [1:0] Off,
  output RamWE,
  output IoWE,
  output IsIO
);

  Comparator #(.width(4), .mode("unsigned")) comparator_1 (.a(Addr[31:28]), .b(4'b1111), .eq(IsIO));  // open: gt, lt
  and and_1 (RamWE, MemWrite, ~IsIO);  // AND_Gate
  and and_2 (IoWE, MemWrite, IsIO);

  assign Off = Addr[1:0];
  assign WordAddr = Addr[13:2];

  // Other names for the same wires on the sheet: top[3:0] = Addr[31:28]

  // Notes on the sheet:
  //   Address Decoder (memory map):
  //   0x0000_0000-0x0000_3FFF : RAM 16 KiB  -> word address = Addr[13:2] (4096 tu 32-bit)
  //   0xF000_0000-0xFFFF_FFFF : I/O (TTY)   -> ghi 1 byte ra man hinh TTY
  //   Addr[1:0] = byte offset trong 1 word (dung cho LB/LH/SB/SH)
  //   Addr[31:28] == 0xF ?
endmodule

module StoreUnit (
  input  [31:0] Old,
  input  [31:0] WData,
  input  [1:0] Off,
  input  [2:0] funct3,
  output [31:0] New
);

  wire [31:0] and_1_out, and_2_out, D, M, multiplexer_1_out;

  Multiplexer #(.width(32), .select(2), .enable("false")) multiplexer_1 (
    .in0(32'hff), .in1(32'hffff), .in2({32{1'b1}}), .in3({32{1'b1}}), .out(multiplexer_1_out),
    .sel(funct3[1:0]));
  Shifter #(.width(32), .shift("ll")) shifter_1 (.in(multiplexer_1_out), .\dist ({Off, 3'b000}), .out(M));
  Shifter #(.width(32), .shift("ll")) shifter_2 (.in(WData), .\dist ({Off, 3'b000}), .out(D));
  assign and_1_out = Old & ~M;  // AND_Gate and_1, 32 bits wide
  assign and_2_out = D & M;  // AND_Gate and_2, 32 bits wide
  assign New = and_1_out | and_2_out;  // OR_Gate or_1, 32 bits wide

  // Other names for the same wires on the sheet: size[1:0] = funct3[1:0]; sh[4:3] = Off

  // Notes on the sheet:
  //   Store Unit (read-modify-write): RAM chi ghi duoc ca word 32-bit,
  //   nen voi SB/SH ta doc word cu (Old), thay dung byte/halfword roi ghi lai ca word.
  //   M = mask (0xFF / 0xFFFF / 0xFFFFFFFF) << sh ;  New = (Old AND ~M) OR ((WData << sh) AND M)
  //   sh = Off * 8 = {Off,000}
  //   size: 00=SB 01=SH 10=SW
  //   Old AND ~M (giu byte khac)
  //   D AND M (byte moi)
endmodule

module LoadUnit (
  input  [31:0] Word,
  input  [1:0] Off,
  input  [2:0] funct3,
  output [31:0] Data
);

  wire [31:0] bit_extender_1_out, bit_extender_2_out, bit_extender_3_out, bit_extender_4_out, S;

  Shifter #(.width(32), .shift("lr")) shifter_1 (.in(Word), .\dist ({Off, 3'b000}), .out(S));
  assign bit_extender_1_out = {{24{S[7]}}, S[7:0]};  // Bit_Extender bit_extender_1
  assign bit_extender_2_out = {{16{S[15]}}, S[15:0]};  // Bit_Extender bit_extender_2
  assign bit_extender_3_out = {{24{1'b0}}, S[7:0]};  // Bit_Extender bit_extender_3
  assign bit_extender_4_out = {{16{1'b0}}, S[15:0]};  // Bit_Extender bit_extender_4
  Multiplexer #(.width(32), .select(3), .enable("false")) multiplexer_1 (
    .in0(bit_extender_1_out), .in1(bit_extender_2_out), .in2(Word), .in3(Word), .in4(bit_extender_3_out),
    .in5(bit_extender_4_out), .in6(Word), .in7(Word), .out(Data), .sel(funct3));

  // Other names for the same wires on the sheet: sh[4:3] = Off

  // Notes on the sheet:
  //   Load Unit: lay byte/halfword tu word doc ra va mo rong dau (sign) hoac them 0 (zero)
  //   Word >> (Off*8) dua byte can lay ve vi tri thap nhat;  funct3 chon: 000 LB, 001 LH, 010 LW, 100 LBU, 101 LHU
  //   sh = Off * 8 = {Off,000}
  //   LB: sign-extend S[7:0]
  //   LH: sign-extend S[15:0]
  //   LBU: zero-extend S[7:0]
  //   LHU: zero-extend S[15:0]
  //   funct3 = 010 (LW): Word
endmodule

module PerfCounters (
  input  CLK,
  input  Run,
  input  Retire,
  output [31:0] cycles,
  output [31:0] instret
);

  wire en_i;
  wire [31:0] adder_1_out, adder_2_out;

  and and_1 (en_i, Run, Retire);
  Adder #(.width(32)) adder_1 (.a(cycles), .b(32'h1), .out(adder_1_out), .cin(1'b0));  // open: cout
  Adder #(.width(32)) adder_2 (.a(instret), .b(32'h1), .out(adder_2_out), .cin(1'b0));  // open: cout
  Register #(.width(32)) u_cycles (.D(adder_1_out), .en(Run), .clk(CLK), .Q(cycles), .clr(1'b0));
  Register #(.width(32)) u_instret (.D(adder_2_out), .en(en_i), .clk(CLK), .Q(instret), .clr(1'b0));

  // Notes on the sheet:
  //   Performance counters: cycles dem moi canh len CLK khi CPU dang chay (Run=1),
  //   instret dem so lenh da hoan thanh (Retire=1).  CPI = cycles / instret
endmodule

module IOController (
  input  [31:0] Addr,
  input  [31:0] WData,
  input  MemWrite,
  input  MemRead,
  input  IsIO,
  input  CLK,
  input  [6:0] KbdData,
  input  KbdAvail,
  input  [7:0] GpioIn,
  output [31:0] IoRData,
  output TxWE,
  output [6:0] TxData,
  output KbdRE,
  output [31:0] GpioOut
);

  wire gpioWE, selGPIO, selRX, selTX;
  wire [31:0] r_gpioin, r_rx;

  Decoder #(.select(3), .enable("true")) decoder_1 (
    .out0(selTX), .out1(selRX), .out4(selGPIO), .sel(Addr[4:2]), .en(IsIO));  // open: out2, out3, out5, out6, out7
  and and_1 (TxWE, MemWrite, selTX);
  and and_2 (KbdRE, MemRead, selRX);
  and and_3 (gpioWE, MemWrite, selGPIO);
  Register #(.width(32)) GPIO_OUT (.D(WData), .en(gpioWE), .clk(CLK), .Q(GpioOut), .clr(1'b0));
  assign r_rx = {{25{1'b0}}, KbdData};  // Bit_Extender bit_extender_1
  assign r_gpioin = {{24{1'b0}}, GpioIn};  // Bit_Extender bit_extender_2
  Multiplexer #(.width(32), .select(3), .enable("false")) multiplexer_1 (
    .in0({32{1'b0}}), .in1(r_rx), .in2({31'h1, KbdAvail}), .in3({32{1'b0}}), .in4(GpioOut), .in5(r_gpioin),
    .in6({32{1'b0}}), .in7({32{1'b0}}), .out(IoRData), .sel(Addr[4:2]));

  assign TxData = WData[6:0];

  // Other names for the same wires on the sheet: idx[2:0] = Addr[4:2]; r_status[0] = KbdAvail

  // Notes on the sheet:
  //   I/O Controller (memory-mapped I/O): thiet bi ngoai vi chi la vai dia chi dac biet
  //   Vung I/O: Addr[31:28] = 0xF.  Thanh ghi I/O chon bang Addr[4:2]:
  //   0xF0000000 UART_TXDATA (W)   0xF0000004 UART_RXDATA (R)   0xF0000008 UART_STATUS (R)
  //   0xF0000010 GPIO_OUT (R/W)    0xF0000014 GPIO_IN (R)       dia chi khac trong vung: doc = 0
  //   Doc RXDATA lay ky tu ra khoi hang doi -> chi bat KbdRE khi la LENH LOAD that (MemRead=1)
  //   idx = Addr[4:2]
  //   chon thanh ghi I/O
  //   STATUS = {0..., 1, KbdAvail}
  //   doc I/O theo idx
endmodule

module IF_ID (
  input  CLK,
  input  EN,
  input  FLUSH,
  input  D_valid,
  input  [31:0] D_pc,
  input  [31:0] D_pc4,
  input  [31:0] D_instr,
  output Q_valid,
  output [31:0] Q_pc,
  output [31:0] Q_pc4,
  output [31:0] Q_instr
);

  wire en_t, multiplexer_1_out;
  wire [31:0] multiplexer_2_out, multiplexer_3_out, multiplexer_4_out;

  Multiplexer #(.width(1), .select(1), .enable("false")) multiplexer_1 (
    .in0(D_valid), .in1(1'b0), .out(multiplexer_1_out), .sel(FLUSH));
  Multiplexer #(.width(32), .select(1), .enable("false")) multiplexer_2 (
    .in0(D_pc), .in1({32{1'b0}}), .out(multiplexer_2_out), .sel(FLUSH));
  Multiplexer #(.width(32), .select(1), .enable("false")) multiplexer_3 (
    .in0(D_pc4), .in1({32{1'b0}}), .out(multiplexer_3_out), .sel(FLUSH));
  Multiplexer #(.width(32), .select(1), .enable("false")) multiplexer_4 (
    .in0(D_instr), .in1({32{1'b0}}), .out(multiplexer_4_out), .sel(FLUSH));
  Register #(.width(1)) valid (.D(multiplexer_1_out), .en(en_t), .clk(CLK), .Q(Q_valid), .clr(1'b0));
  Register #(.width(32)) pc (.D(multiplexer_2_out), .en(en_t), .clk(CLK), .Q(Q_pc), .clr(1'b0));
  Register #(.width(32)) pc4 (.D(multiplexer_3_out), .en(en_t), .clk(CLK), .Q(Q_pc4), .clr(1'b0));
  Register #(.width(32)) instr (.D(multiplexer_4_out), .en(en_t), .clk(CLK), .Q(Q_instr), .clr(1'b0));
  or or_1 (en_t, EN, FLUSH);

  // Notes on the sheet:
  //   Pipeline register IF/ID: luu toan bo thong tin cua 1 lenh giua 2 tang
  //   EN = 0  -> giu nguyen gia tri (stall).   FLUSH = 1 -> nap 0 (bien lenh thanh bubble/NOP)
  //   Moi gia tri 0 = an toan: valid=0, instr=0 (khong phai lenh hop le), moi tin hieu dieu khien = 0
  //   en_eff = EN OR FLUSH (flush phai thang duoc ca stall)
endmodule

module ID_EX (
  input  CLK,
  input  EN,
  input  FLUSH,
  input  D_valid,
  input  [31:0] D_pc,
  input  [31:0] D_pc4,
  input  [31:0] D_instr,
  input  [31:0] D_rs1d,
  input  [31:0] D_rs2d,
  input  [31:0] D_imm,
  input  [4:0] D_rs1,
  input  [4:0] D_rs2,
  input  [4:0] D_rd,
  input  [2:0] D_funct3,
  input  [3:0] D_ALUCtrl,
  input  [1:0] D_ASel,
  input  D_BSel,
  input  D_RegWrite,
  input  D_MemRead,
  input  D_MemWrite,
  input  [1:0] D_WBSel,
  input  D_Branch,
  input  D_Jal,
  input  D_Jalr,
  input  D_Halt,
  output Q_valid,
  output [31:0] Q_pc,
  output [31:0] Q_pc4,
  output [31:0] Q_instr,
  output [31:0] Q_rs1d,
  output [31:0] Q_rs2d,
  output [31:0] Q_imm,
  output [4:0] Q_rs1,
  output [4:0] Q_rs2,
  output [4:0] Q_rd,
  output [2:0] Q_funct3,
  output [3:0] Q_ALUCtrl,
  output [1:0] Q_ASel,
  output Q_BSel,
  output Q_RegWrite,
  output Q_MemRead,
  output Q_MemWrite,
  output [1:0] Q_WBSel,
  output Q_Branch,
  output Q_Jal,
  output Q_Jalr,
  output Q_Halt
);

  wire en_t, multiplexer_1_out, multiplexer_14_out, multiplexer_15_out, multiplexer_16_out,
       multiplexer_17_out, multiplexer_19_out, multiplexer_20_out, multiplexer_21_out, multiplexer_22_out;
  wire [1:0] multiplexer_13_out, multiplexer_18_out;
  wire [2:0] multiplexer_11_out;
  wire [3:0] multiplexer_12_out;
  wire [4:0] multiplexer_8_out, multiplexer_9_out, multiplexer_10_out;
  wire [31:0] multiplexer_2_out, multiplexer_3_out, multiplexer_4_out, multiplexer_5_out, multiplexer_6_out,
       multiplexer_7_out;

  Multiplexer #(.width(1), .select(1), .enable("false")) multiplexer_1 (
    .in0(D_valid), .in1(1'b0), .out(multiplexer_1_out), .sel(FLUSH));
  Multiplexer #(.width(32), .select(1), .enable("false")) multiplexer_2 (
    .in0(D_pc), .in1({32{1'b0}}), .out(multiplexer_2_out), .sel(FLUSH));
  Multiplexer #(.width(32), .select(1), .enable("false")) multiplexer_3 (
    .in0(D_pc4), .in1({32{1'b0}}), .out(multiplexer_3_out), .sel(FLUSH));
  Multiplexer #(.width(32), .select(1), .enable("false")) multiplexer_4 (
    .in0(D_instr), .in1({32{1'b0}}), .out(multiplexer_4_out), .sel(FLUSH));
  Multiplexer #(.width(32), .select(1), .enable("false")) multiplexer_5 (
    .in0(D_rs1d), .in1({32{1'b0}}), .out(multiplexer_5_out), .sel(FLUSH));
  Multiplexer #(.width(32), .select(1), .enable("false")) multiplexer_6 (
    .in0(D_rs2d), .in1({32{1'b0}}), .out(multiplexer_6_out), .sel(FLUSH));
  Multiplexer #(.width(32), .select(1), .enable("false")) multiplexer_7 (
    .in0(D_imm), .in1({32{1'b0}}), .out(multiplexer_7_out), .sel(FLUSH));
  Multiplexer #(.width(5), .select(1), .enable("false")) multiplexer_8 (
    .in0(D_rs1), .in1({5{1'b0}}), .out(multiplexer_8_out), .sel(FLUSH));
  Multiplexer #(.width(5), .select(1), .enable("false")) multiplexer_9 (
    .in0(D_rs2), .in1({5{1'b0}}), .out(multiplexer_9_out), .sel(FLUSH));
  Multiplexer #(.width(5), .select(1), .enable("false")) multiplexer_10 (
    .in0(D_rd), .in1({5{1'b0}}), .out(multiplexer_10_out), .sel(FLUSH));
  Multiplexer #(.width(3), .select(1), .enable("false")) multiplexer_11 (
    .in0(D_funct3), .in1(3'b000), .out(multiplexer_11_out), .sel(FLUSH));
  Multiplexer #(.width(4), .select(1), .enable("false")) multiplexer_12 (
    .in0(D_ALUCtrl), .in1(4'b0000), .out(multiplexer_12_out), .sel(FLUSH));
  Multiplexer #(.width(2), .select(1), .enable("false")) multiplexer_13 (
    .in0(D_ASel), .in1(2'b00), .out(multiplexer_13_out), .sel(FLUSH));
  Multiplexer #(.width(1), .select(1), .enable("false")) multiplexer_14 (
    .in0(D_BSel), .in1(1'b0), .out(multiplexer_14_out), .sel(FLUSH));
  Multiplexer #(.width(1), .select(1), .enable("false")) multiplexer_15 (
    .in0(D_RegWrite), .in1(1'b0), .out(multiplexer_15_out), .sel(FLUSH));
  Multiplexer #(.width(1), .select(1), .enable("false")) multiplexer_16 (
    .in0(D_MemRead), .in1(1'b0), .out(multiplexer_16_out), .sel(FLUSH));
  Multiplexer #(.width(1), .select(1), .enable("false")) multiplexer_17 (
    .in0(D_MemWrite), .in1(1'b0), .out(multiplexer_17_out), .sel(FLUSH));
  Multiplexer #(.width(2), .select(1), .enable("false")) multiplexer_18 (
    .in0(D_WBSel), .in1(2'b00), .out(multiplexer_18_out), .sel(FLUSH));
  Multiplexer #(.width(1), .select(1), .enable("false")) multiplexer_19 (
    .in0(D_Branch), .in1(1'b0), .out(multiplexer_19_out), .sel(FLUSH));
  Multiplexer #(.width(1), .select(1), .enable("false")) multiplexer_20 (
    .in0(D_Jal), .in1(1'b0), .out(multiplexer_20_out), .sel(FLUSH));
  Multiplexer #(.width(1), .select(1), .enable("false")) multiplexer_21 (
    .in0(D_Jalr), .in1(1'b0), .out(multiplexer_21_out), .sel(FLUSH));
  Multiplexer #(.width(1), .select(1), .enable("false")) multiplexer_22 (
    .in0(D_Halt), .in1(1'b0), .out(multiplexer_22_out), .sel(FLUSH));
  Register #(.width(1)) valid (.D(multiplexer_1_out), .en(en_t), .clk(CLK), .Q(Q_valid), .clr(1'b0));
  Register #(.width(32)) pc (.D(multiplexer_2_out), .en(en_t), .clk(CLK), .Q(Q_pc), .clr(1'b0));
  Register #(.width(32)) pc4 (.D(multiplexer_3_out), .en(en_t), .clk(CLK), .Q(Q_pc4), .clr(1'b0));
  Register #(.width(32)) instr (.D(multiplexer_4_out), .en(en_t), .clk(CLK), .Q(Q_instr), .clr(1'b0));
  Register #(.width(32)) rs1d (.D(multiplexer_5_out), .en(en_t), .clk(CLK), .Q(Q_rs1d), .clr(1'b0));
  Register #(.width(32)) rs2d (.D(multiplexer_6_out), .en(en_t), .clk(CLK), .Q(Q_rs2d), .clr(1'b0));
  Register #(.width(32)) imm (.D(multiplexer_7_out), .en(en_t), .clk(CLK), .Q(Q_imm), .clr(1'b0));
  Register #(.width(5)) rs1 (.D(multiplexer_8_out), .en(en_t), .clk(CLK), .Q(Q_rs1), .clr(1'b0));
  Register #(.width(5)) rs2 (.D(multiplexer_9_out), .en(en_t), .clk(CLK), .Q(Q_rs2), .clr(1'b0));
  Register #(.width(5)) rd (.D(multiplexer_10_out), .en(en_t), .clk(CLK), .Q(Q_rd), .clr(1'b0));
  Register #(.width(3)) funct3 (.D(multiplexer_11_out), .en(en_t), .clk(CLK), .Q(Q_funct3), .clr(1'b0));
  Register #(.width(4)) ALUCtrl (.D(multiplexer_12_out), .en(en_t), .clk(CLK), .Q(Q_ALUCtrl), .clr(1'b0));
  Register #(.width(2)) ASel (.D(multiplexer_13_out), .en(en_t), .clk(CLK), .Q(Q_ASel), .clr(1'b0));
  Register #(.width(1)) BSel (.D(multiplexer_14_out), .en(en_t), .clk(CLK), .Q(Q_BSel), .clr(1'b0));
  Register #(.width(1)) RegWrite (.D(multiplexer_15_out), .en(en_t), .clk(CLK), .Q(Q_RegWrite), .clr(1'b0));
  Register #(.width(1)) MemRead (.D(multiplexer_16_out), .en(en_t), .clk(CLK), .Q(Q_MemRead), .clr(1'b0));
  Register #(.width(1)) MemWrite (.D(multiplexer_17_out), .en(en_t), .clk(CLK), .Q(Q_MemWrite), .clr(1'b0));
  Register #(.width(2)) WBSel (.D(multiplexer_18_out), .en(en_t), .clk(CLK), .Q(Q_WBSel), .clr(1'b0));
  Register #(.width(1)) Branch (.D(multiplexer_19_out), .en(en_t), .clk(CLK), .Q(Q_Branch), .clr(1'b0));
  Register #(.width(1)) Jal (.D(multiplexer_20_out), .en(en_t), .clk(CLK), .Q(Q_Jal), .clr(1'b0));
  Register #(.width(1)) Jalr (.D(multiplexer_21_out), .en(en_t), .clk(CLK), .Q(Q_Jalr), .clr(1'b0));
  Register #(.width(1)) Halt (.D(multiplexer_22_out), .en(en_t), .clk(CLK), .Q(Q_Halt), .clr(1'b0));
  or or_1 (en_t, EN, FLUSH);

  // Notes on the sheet:
  //   Pipeline register ID/EX: luu toan bo thong tin cua 1 lenh giua 2 tang
  //   EN = 0  -> giu nguyen gia tri (stall).   FLUSH = 1 -> nap 0 (bien lenh thanh bubble/NOP)
  //   Moi gia tri 0 = an toan: valid=0, instr=0 (khong phai lenh hop le), moi tin hieu dieu khien = 0
  //   en_eff = EN OR FLUSH (flush phai thang duoc ca stall)
endmodule

module EX_MEM (
  input  CLK,
  input  EN,
  input  FLUSH,
  input  D_valid,
  input  [31:0] D_pc,
  input  [31:0] D_instr,
  input  [31:0] D_exres,
  input  [31:0] D_sdata,
  input  [4:0] D_rd,
  input  [2:0] D_funct3,
  input  D_RegWrite,
  input  D_MemRead,
  input  D_MemWrite,
  input  D_MemToReg,
  input  D_Halt,
  output Q_valid,
  output [31:0] Q_pc,
  output [31:0] Q_instr,
  output [31:0] Q_exres,
  output [31:0] Q_sdata,
  output [4:0] Q_rd,
  output [2:0] Q_funct3,
  output Q_RegWrite,
  output Q_MemRead,
  output Q_MemWrite,
  output Q_MemToReg,
  output Q_Halt
);

  wire en_t, multiplexer_1_out, multiplexer_8_out, multiplexer_9_out, multiplexer_10_out, multiplexer_11_out,
       multiplexer_12_out;
  wire [2:0] multiplexer_7_out;
  wire [4:0] multiplexer_6_out;
  wire [31:0] multiplexer_2_out, multiplexer_3_out, multiplexer_4_out, multiplexer_5_out;

  Multiplexer #(.width(1), .select(1), .enable("false")) multiplexer_1 (
    .in0(D_valid), .in1(1'b0), .out(multiplexer_1_out), .sel(FLUSH));
  Multiplexer #(.width(32), .select(1), .enable("false")) multiplexer_2 (
    .in0(D_pc), .in1({32{1'b0}}), .out(multiplexer_2_out), .sel(FLUSH));
  Multiplexer #(.width(32), .select(1), .enable("false")) multiplexer_3 (
    .in0(D_instr), .in1({32{1'b0}}), .out(multiplexer_3_out), .sel(FLUSH));
  Multiplexer #(.width(32), .select(1), .enable("false")) multiplexer_4 (
    .in0(D_exres), .in1({32{1'b0}}), .out(multiplexer_4_out), .sel(FLUSH));
  Multiplexer #(.width(32), .select(1), .enable("false")) multiplexer_5 (
    .in0(D_sdata), .in1({32{1'b0}}), .out(multiplexer_5_out), .sel(FLUSH));
  Multiplexer #(.width(5), .select(1), .enable("false")) multiplexer_6 (
    .in0(D_rd), .in1({5{1'b0}}), .out(multiplexer_6_out), .sel(FLUSH));
  Multiplexer #(.width(3), .select(1), .enable("false")) multiplexer_7 (
    .in0(D_funct3), .in1(3'b000), .out(multiplexer_7_out), .sel(FLUSH));
  Multiplexer #(.width(1), .select(1), .enable("false")) multiplexer_8 (
    .in0(D_RegWrite), .in1(1'b0), .out(multiplexer_8_out), .sel(FLUSH));
  Multiplexer #(.width(1), .select(1), .enable("false")) multiplexer_9 (
    .in0(D_MemRead), .in1(1'b0), .out(multiplexer_9_out), .sel(FLUSH));
  Multiplexer #(.width(1), .select(1), .enable("false")) multiplexer_10 (
    .in0(D_MemWrite), .in1(1'b0), .out(multiplexer_10_out), .sel(FLUSH));
  Multiplexer #(.width(1), .select(1), .enable("false")) multiplexer_11 (
    .in0(D_MemToReg), .in1(1'b0), .out(multiplexer_11_out), .sel(FLUSH));
  Multiplexer #(.width(1), .select(1), .enable("false")) multiplexer_12 (
    .in0(D_Halt), .in1(1'b0), .out(multiplexer_12_out), .sel(FLUSH));
  Register #(.width(1)) valid (.D(multiplexer_1_out), .en(en_t), .clk(CLK), .Q(Q_valid), .clr(1'b0));
  Register #(.width(32)) pc (.D(multiplexer_2_out), .en(en_t), .clk(CLK), .Q(Q_pc), .clr(1'b0));
  Register #(.width(32)) instr (.D(multiplexer_3_out), .en(en_t), .clk(CLK), .Q(Q_instr), .clr(1'b0));
  Register #(.width(32)) exres (.D(multiplexer_4_out), .en(en_t), .clk(CLK), .Q(Q_exres), .clr(1'b0));
  Register #(.width(32)) sdata (.D(multiplexer_5_out), .en(en_t), .clk(CLK), .Q(Q_sdata), .clr(1'b0));
  Register #(.width(5)) rd (.D(multiplexer_6_out), .en(en_t), .clk(CLK), .Q(Q_rd), .clr(1'b0));
  Register #(.width(3)) funct3 (.D(multiplexer_7_out), .en(en_t), .clk(CLK), .Q(Q_funct3), .clr(1'b0));
  Register #(.width(1)) RegWrite (.D(multiplexer_8_out), .en(en_t), .clk(CLK), .Q(Q_RegWrite), .clr(1'b0));
  Register #(.width(1)) MemRead (.D(multiplexer_9_out), .en(en_t), .clk(CLK), .Q(Q_MemRead), .clr(1'b0));
  Register #(.width(1)) MemWrite (.D(multiplexer_10_out), .en(en_t), .clk(CLK), .Q(Q_MemWrite), .clr(1'b0));
  Register #(.width(1)) MemToReg (.D(multiplexer_11_out), .en(en_t), .clk(CLK), .Q(Q_MemToReg), .clr(1'b0));
  Register #(.width(1)) Halt (.D(multiplexer_12_out), .en(en_t), .clk(CLK), .Q(Q_Halt), .clr(1'b0));
  or or_1 (en_t, EN, FLUSH);

  // Notes on the sheet:
  //   Pipeline register EX/MEM: luu toan bo thong tin cua 1 lenh giua 2 tang
  //   EN = 0  -> giu nguyen gia tri (stall).   FLUSH = 1 -> nap 0 (bien lenh thanh bubble/NOP)
  //   Moi gia tri 0 = an toan: valid=0, instr=0 (khong phai lenh hop le), moi tin hieu dieu khien = 0
  //   en_eff = EN OR FLUSH (flush phai thang duoc ca stall)
endmodule

module MEM_WB (
  input  CLK,
  input  EN,
  input  FLUSH,
  input  D_valid,
  input  [31:0] D_pc,
  input  [31:0] D_instr,
  input  [31:0] D_exres,
  input  [31:0] D_mdata,
  input  [4:0] D_rd,
  input  D_RegWrite,
  input  D_MemToReg,
  input  D_Halt,
  output Q_valid,
  output [31:0] Q_pc,
  output [31:0] Q_instr,
  output [31:0] Q_exres,
  output [31:0] Q_mdata,
  output [4:0] Q_rd,
  output Q_RegWrite,
  output Q_MemToReg,
  output Q_Halt
);

  wire en_t, multiplexer_1_out, multiplexer_7_out, multiplexer_8_out, multiplexer_9_out;
  wire [4:0] multiplexer_6_out;
  wire [31:0] multiplexer_2_out, multiplexer_3_out, multiplexer_4_out, multiplexer_5_out;

  Multiplexer #(.width(1), .select(1), .enable("false")) multiplexer_1 (
    .in0(D_valid), .in1(1'b0), .out(multiplexer_1_out), .sel(FLUSH));
  Multiplexer #(.width(32), .select(1), .enable("false")) multiplexer_2 (
    .in0(D_pc), .in1({32{1'b0}}), .out(multiplexer_2_out), .sel(FLUSH));
  Multiplexer #(.width(32), .select(1), .enable("false")) multiplexer_3 (
    .in0(D_instr), .in1({32{1'b0}}), .out(multiplexer_3_out), .sel(FLUSH));
  Multiplexer #(.width(32), .select(1), .enable("false")) multiplexer_4 (
    .in0(D_exres), .in1({32{1'b0}}), .out(multiplexer_4_out), .sel(FLUSH));
  Multiplexer #(.width(32), .select(1), .enable("false")) multiplexer_5 (
    .in0(D_mdata), .in1({32{1'b0}}), .out(multiplexer_5_out), .sel(FLUSH));
  Multiplexer #(.width(5), .select(1), .enable("false")) multiplexer_6 (
    .in0(D_rd), .in1({5{1'b0}}), .out(multiplexer_6_out), .sel(FLUSH));
  Multiplexer #(.width(1), .select(1), .enable("false")) multiplexer_7 (
    .in0(D_RegWrite), .in1(1'b0), .out(multiplexer_7_out), .sel(FLUSH));
  Multiplexer #(.width(1), .select(1), .enable("false")) multiplexer_8 (
    .in0(D_MemToReg), .in1(1'b0), .out(multiplexer_8_out), .sel(FLUSH));
  Multiplexer #(.width(1), .select(1), .enable("false")) multiplexer_9 (
    .in0(D_Halt), .in1(1'b0), .out(multiplexer_9_out), .sel(FLUSH));
  Register #(.width(1)) valid (.D(multiplexer_1_out), .en(en_t), .clk(CLK), .Q(Q_valid), .clr(1'b0));
  Register #(.width(32)) pc (.D(multiplexer_2_out), .en(en_t), .clk(CLK), .Q(Q_pc), .clr(1'b0));
  Register #(.width(32)) instr (.D(multiplexer_3_out), .en(en_t), .clk(CLK), .Q(Q_instr), .clr(1'b0));
  Register #(.width(32)) exres (.D(multiplexer_4_out), .en(en_t), .clk(CLK), .Q(Q_exres), .clr(1'b0));
  Register #(.width(32)) mdata (.D(multiplexer_5_out), .en(en_t), .clk(CLK), .Q(Q_mdata), .clr(1'b0));
  Register #(.width(5)) rd (.D(multiplexer_6_out), .en(en_t), .clk(CLK), .Q(Q_rd), .clr(1'b0));
  Register #(.width(1)) RegWrite (.D(multiplexer_7_out), .en(en_t), .clk(CLK), .Q(Q_RegWrite), .clr(1'b0));
  Register #(.width(1)) MemToReg (.D(multiplexer_8_out), .en(en_t), .clk(CLK), .Q(Q_MemToReg), .clr(1'b0));
  Register #(.width(1)) Halt (.D(multiplexer_9_out), .en(en_t), .clk(CLK), .Q(Q_Halt), .clr(1'b0));
  or or_1 (en_t, EN, FLUSH);

  // Notes on the sheet:
  //   Pipeline register MEM/WB: luu toan bo thong tin cua 1 lenh giua 2 tang
  //   EN = 0  -> giu nguyen gia tri (stall).   FLUSH = 1 -> nap 0 (bien lenh thanh bubble/NOP)
  //   Moi gia tri 0 = an toan: valid=0, instr=0 (khong phai lenh hop le), moi tin hieu dieu khien = 0
  //   en_eff = EN OR FLUSH (flush phai thang duoc ca stall)
endmodule

module ForwardUnit (
  input  [4:0] rs1,
  input  [4:0] rs2,
  input  [4:0] M_rd,
  input  M_RegWrite,
  input  [4:0] W_rd,
  input  W_RegWrite,
  output [1:0] FwdA,
  output [1:0] FwdB
);

  wire comparator_1_eq, comparator_2_gt, comparator_3_eq, comparator_4_gt, comparator_5_eq, comparator_6_gt,
       comparator_7_eq, comparator_8_gt, Meq1, Meq2, Weq1, Weq2, Whit1, Whit2;

  Comparator #(.width(5), .mode("unsigned")) comparator_1 (.a(M_rd), .b(rs1), .eq(comparator_1_eq));  // open: gt, lt
  Comparator #(.width(5), .mode("unsigned")) comparator_2 (
    .a(M_rd), .b({5{1'b0}}), .gt(comparator_2_gt));  // open: eq, lt
  Comparator #(.width(5), .mode("unsigned")) comparator_3 (.a(W_rd), .b(rs1), .eq(comparator_3_eq));  // open: gt, lt
  Comparator #(.width(5), .mode("unsigned")) comparator_4 (
    .a(W_rd), .b({5{1'b0}}), .gt(comparator_4_gt));  // open: eq, lt
  Comparator #(.width(5), .mode("unsigned")) comparator_5 (.a(M_rd), .b(rs2), .eq(comparator_5_eq));  // open: gt, lt
  Comparator #(.width(5), .mode("unsigned")) comparator_6 (
    .a(M_rd), .b({5{1'b0}}), .gt(comparator_6_gt));  // open: eq, lt
  Comparator #(.width(5), .mode("unsigned")) comparator_7 (.a(W_rd), .b(rs2), .eq(comparator_7_eq));  // open: gt, lt
  Comparator #(.width(5), .mode("unsigned")) comparator_8 (
    .a(W_rd), .b({5{1'b0}}), .gt(comparator_8_gt));  // open: eq, lt
  and and_1 (Meq1, comparator_1_eq, comparator_2_gt);
  and and_2 (Weq1, comparator_3_eq, comparator_4_gt);
  and and_3 (Meq2, comparator_5_eq, comparator_6_gt);
  and and_4 (Weq2, comparator_7_eq, comparator_8_gt);
  and and_5 (FwdA[0], Meq1, M_RegWrite);
  and and_6 (Whit1, Weq1, W_RegWrite);
  and and_7 (FwdB[0], Meq2, M_RegWrite);
  and and_8 (Whit2, Weq2, W_RegWrite);
  and and_9 (FwdA[1], Whit1, ~FwdA[0]);  // AND_Gate
  and and_10 (FwdB[1], Whit2, ~FwdB[0]);  // AND_Gate

  // Other names for the same wires on the sheet: Mhit1 = FwdA[0]; Mhit2 = FwdB[0]

  // Notes on the sheet:
  //   Forwarding Unit (bypass): lay ket qua chua kip ghi vao Register File
  //   FwdA/FwdB: 00 = gia tri doc tu ID/EX,  01 = tu EX/MEM (lenh truoc 1 lenh),  10 = tu MEM/WB (truoc 2 lenh)
  //   Dieu kien: lenh truoc co RegWrite=1, rd != 0 va rd == rs.  EX/MEM uu tien hon (moi hon).
  //   bit0 = MEM hit, bit1 = WB hit AND NOT MEM hit
endmodule

module HazardUnit (
  input  [4:0] rs1,
  input  [4:0] rs2,
  input  UseRs1,
  input  UseRs2,
  input  D_Halt,
  input  [4:0] E_rd,
  input  E_MemRead,
  input  Redirect,
  output PCWrite,
  output IFID_Write,
  output IFID_Flush,
  output IDEX_Flush,
  output Stall,
  output LoadUse
);

  wire and_3_out, and_4_out, comparator_1_eq, comparator_2_gt, comparator_3_eq, comparator_4_gt, h1, h2,
       or_4_out;

  Comparator #(.width(5), .mode("unsigned")) comparator_1 (.a(E_rd), .b(rs1), .eq(comparator_1_eq));  // open: gt, lt
  Comparator #(.width(5), .mode("unsigned")) comparator_2 (
    .a(E_rd), .b({5{1'b0}}), .gt(comparator_2_gt));  // open: eq, lt
  Comparator #(.width(5), .mode("unsigned")) comparator_3 (.a(E_rd), .b(rs2), .eq(comparator_3_eq));  // open: gt, lt
  Comparator #(.width(5), .mode("unsigned")) comparator_4 (
    .a(E_rd), .b({5{1'b0}}), .gt(comparator_4_gt));  // open: eq, lt
  and and_1 (h1, comparator_1_eq, comparator_2_gt);
  and and_2 (h2, comparator_3_eq, comparator_4_gt);
  and and_3 (and_3_out, h1, UseRs1);
  and and_4 (and_4_out, h2, UseRs2);
  or or_1 (Stall, LoadUse, D_Halt);
  or or_2 (IFID_Write, ~Stall, Redirect);  // OR_Gate
  or or_3 (IDEX_Flush, Redirect, LoadUse);
  or or_4 (or_4_out, and_3_out, and_4_out);
  and and_5 (LoadUse, or_4_out, E_MemRead);

  assign IFID_Flush = Redirect;
  assign PCWrite = IFID_Write;

  // Notes on the sheet:
  //   Hazard Detection Unit
  //   Load-use: lenh o EX la LOAD (MemRead) va lenh o ID can doc dung thanh ghi do -> chen 1 bubble
  //     (forwarding khong cuu duoc vi du lieu load chi co o cuoi tang MEM)
  //   Control hazard: branch/jump duoc giai quyet o EX; neu nhay (Redirect=1) -> xoa 2 lenh da nap sai (IF/ID, ID/EX)
  //   Halt o ID: dung nap lenh, cho EBREAK chay toi WB (khi do moi lenh truoc da xong)
  //   PCWrite = IFID_Write = !Stall | Redirect
  //   IDEX_Flush = Redirect | LoadUse (chen bubble)
  //   LoadUse
endmodule

module IDBypass (
  input  [31:0] RD1,
  input  [31:0] RD2,
  input  [4:0] rs1,
  input  [4:0] rs2,
  input  [4:0] W_rd,
  input  W_RegWrite,
  input  [31:0] W_data,
  output [31:0] O1,
  output [31:0] O2
);

  wire and_3_out, and_4_out, comparator_1_eq, comparator_2_gt, comparator_3_eq, comparator_4_gt, eq1, eq2;

  Comparator #(.width(5), .mode("unsigned")) comparator_1 (.a(W_rd), .b(rs1), .eq(comparator_1_eq));  // open: gt, lt
  Comparator #(.width(5), .mode("unsigned")) comparator_2 (
    .a(W_rd), .b({5{1'b0}}), .gt(comparator_2_gt));  // open: eq, lt
  Comparator #(.width(5), .mode("unsigned")) comparator_3 (.a(W_rd), .b(rs2), .eq(comparator_3_eq));  // open: gt, lt
  Comparator #(.width(5), .mode("unsigned")) comparator_4 (
    .a(W_rd), .b({5{1'b0}}), .gt(comparator_4_gt));  // open: eq, lt
  and and_1 (eq1, comparator_1_eq, comparator_2_gt);
  and and_2 (eq2, comparator_3_eq, comparator_4_gt);
  and and_3 (and_3_out, eq1, W_RegWrite);
  and and_4 (and_4_out, eq2, W_RegWrite);
  Multiplexer #(.width(32), .select(1), .enable("false")) multiplexer_1 (
    .in0(RD1), .in1(W_data), .out(O1), .sel(and_3_out));
  Multiplexer #(.width(32), .select(1), .enable("false")) multiplexer_2 (
    .in0(RD2), .in1(W_data), .out(O2), .sel(and_4_out));

  // Notes on the sheet:
  //   WB -> ID bypass (write-through Register File)
  //   Lenh o WB ghi thanh ghi o CANH LEN cuoi chu ky, nhung lenh o ID doc ngay trong chu ky do
  //   -> neu cung thanh ghi thi lay thang du lieu dang ghi (W_data) thay vi gia tri cu.
endmodule
